// Logisim project CS1409_U201414800_刘一龙_alu.circ as structural Verilog: 9 circuits, main circuit ALU
module ALU (
  input  [31:0] X,
  input  [31:0] Y,
  input  [3:0] AluOP,
  output Signed_Overflow,
  output UnSigned_Overflow,
  output Equal,
  output [31:0] Result,
  output [31:0] Result_2
);

  wire adder32_1_cout, and_2_out, and_3_out, and_4_out, and_5_out, comparator_1_lt, comparator_2_lt,
       not_2_out, not_3_out, or_2_out, or_3_out, S_f_out, Suber_cout, X_f_out, Y_f_out;
  wire [31:0] adder32_1_s, and_1_out, bit_extender_1_out, bit_extender_2_out, divider_1_out, divider_1_rem,
       multiplier_1_cout, multiplier_1_out, nor_1_out, not_1_out, or_1_out, shifter_1_out, shifter_2_out,
       shifter_3_out, Suber_s, xor_1_out;

  // Probe on X
  // Probe on X
  // Probe on Y
  // Probe on Y
  // Probe on AluOP
  // Probe on Result
  // Probe on Result
  not Y_f (Y_f_out, Y[31]);
  not X_f (X_f_out, X[31]);
  assign not_1_out = ~Y;  // NOT_Gate not_1, 32 bits wide
  // Probe on Result_2
  not S_f (S_f_out, adder32_1_s[31]);
  Shifter #(.width(32)) shifter_1 (.in(X), .\dist (Y[4:0]), .out(shifter_1_out));
  Shifter #(.width(32), .shift("ar")) shifter_2 (.in(X), .\dist (Y[4:0]), .out(shifter_2_out));
  Shifter #(.width(32), .shift("lr")) shifter_3 (.in(X), .\dist (Y[4:0]), .out(shifter_3_out));
  Multiplier #(.width(32)) multiplier_1 (
    .a(X), .b(Y), .out(multiplier_1_out), .cin({32{1'b0}}), .cout(multiplier_1_cout));
  Divider #(.width(32)) divider_1 (.a(X), .b(Y), .out(divider_1_out), .upper({32{1'b0}}), .rem(divider_1_rem));
  Adder32 adder32_1 (.C0(1'b0), .Cout(adder32_1_cout), .S(adder32_1_s), .X(X), .Y(Y));
  Adder32 Suber (.C0(1'b1), .Cout(Suber_cout), .S(Suber_s), .X(X), .Y(not_1_out));
  assign and_1_out = X & Y;  // AND_Gate and_1, 32 bits wide
  assign or_1_out = X | Y;  // OR_Gate or_1, 32 bits wide
  assign xor_1_out = X ^ Y;  // XOR_Gate xor_1, 32 bits wide
  assign nor_1_out = ~(X | Y);  // NOR_Gate nor_1, 32 bits wide
  Comparator #(.width(32)) comparator_1 (.a(X), .b(Y), .eq(Equal), .lt(comparator_1_lt));  // open: gt
  Comparator #(.width(32), .mode("unsigned")) comparator_2 (.a(X), .b(Y), .lt(comparator_2_lt));  // open: gt, eq
  and and_2 (and_2_out, X[31], Y[31], S_f_out);
  and and_3 (and_3_out, X_f_out, Y_f_out, adder32_1_s[31]);
  not not_2 (not_2_out, Suber_s[31]);
  assign bit_extender_1_out = {{31{1'b0}}, comparator_1_lt};  // Bit_Extender bit_extender_1
  assign bit_extender_2_out = {{31{1'b0}}, comparator_2_lt};  // Bit_Extender bit_extender_2
  or or_2 (or_2_out, and_2_out, and_3_out);
  and and_4 (and_4_out, X[31], Y_f_out, not_2_out);
  and and_5 (and_5_out, X_f_out, Y[31], Suber_s[31]);
  or or_3 (or_3_out, and_4_out, and_5_out);
  not not_3 (not_3_out, Suber_cout);
  Multiplexer #(.select(4), .enable("false")) multiplexer_1 (
    .in0(1'b0), .in1(1'b0), .in2(1'b0), .in3(1'b0), .in4(1'b0), .in5(adder32_1_cout), .in6(not_3_out),
    .in7(1'b0), .in8(1'b0), .in9(1'b0), .in10(1'b0), .in11(1'b0), .in12(1'b0), .in13(1'b0), .in14(1'b0),
    .in15(1'b0), .out(UnSigned_Overflow), .sel(AluOP));
  Multiplexer #(.select(4), .enable("false")) multiplexer_2 (
    .in0(1'b0), .in1(1'b0), .in2(1'b0), .in3(1'b0), .in4(1'b0), .in5(or_2_out), .in6(or_3_out), .in7(1'b0),
    .in8(1'b0), .in9(1'b0), .in10(1'b0), .in11(1'b0), .in12(1'b0), .in13(1'b0), .in14(1'b0), .in15(1'b0),
    .out(Signed_Overflow), .sel(AluOP));
  Multiplexer #(.select(4), .width(32), .enable("false")) multiplexer_3 (
    .in0(shifter_1_out), .in1(shifter_2_out), .in2(shifter_3_out), .in3(multiplier_1_out),
    .in4(divider_1_out), .in5(adder32_1_s), .in6(Suber_s), .in7(and_1_out), .in8(or_1_out), .in9(xor_1_out),
    .in10(nor_1_out), .in11(bit_extender_1_out), .in12(bit_extender_2_out), .in13({32{1'b0}}),
    .in14({32{1'b0}}), .in15({32{1'b0}}), .out(Result), .sel(AluOP));
  Multiplexer #(.select(4), .width(32), .enable("false")) multiplexer_4 (
    .in0({32{1'b0}}), .in1({32{1'b0}}), .in2({32{1'b0}}), .in3(multiplier_1_cout), .in4(divider_1_rem),
    .in5({32{1'b0}}), .in6({32{1'b0}}), .in7({32{1'b0}}), .in8({32{1'b0}}), .in9({32{1'b0}}),
    .in10({32{1'b0}}), .in11({32{1'b0}}), .in12({32{1'b0}}), .in13({32{1'b0}}), .in14({32{1'b0}}),
    .in15({32{1'b0}}), .out(Result_2), .sel(AluOP));

  // Other names for the same wires on the sheet: OF = Signed_Overflow; Result2[31:0] = Result_2; S[3:0] = AluOP;
  //   UOF = UnSigned_Overflow

  // Notes on the sheet:
  //   不要改变此引脚区域内容，也不要改变ALU封装形式
  //   输入引脚
  //   请在下方利用上方输入输出引脚的隧道信号构建ALU电路，ctrl+d复制选择部件
  //   华中科技大学计算机学院 计算机组成原理，鸣谢加州大学伯克利CS61C课程
  //   输出引脚
  //   探测区域
  //   Add: OF = (X_f & Y_f & !S_f)|(!X_f & !Y_f & S_f)
  //   Sub: OF  = (X_f & !Y_f & !S_f)|(!X_f & Y_f & S_f)
endmodule

module \演示电路  (
  input  [31:0] X,
  input  [31:0] Y,
  input  [3:0] ALUOP,
  output Signed_Overflow,
  output Unsigned_overflow,
  output [31:0] Result,
  output [31:0] Result_2,
  output Equal
);

  // Probe on X
  // Probe on X
  ALU alu_1 (
    .AluOP(ALUOP), .X(X), .Equal(Equal), .Result(Result), .Signed_Overflow(Signed_Overflow), .Y(Y),
    .Result_2(Result_2), .UnSigned_Overflow(Unsigned_overflow));
  // Probe on ALUOP
  // Probe on Y
  // Probe on Y
  // Probe on Result
  // Probe on Result
  // Probe on Result_2

  // Notes on the sheet:
  //   ALu电路无需调整位置即可连接在该电路中，并且不能出现蓝色线缆和三态输出
endmodule

module \等差数列  (
  input  [31:0] \数列初始值 ,
  input  [31:0] \等差值 ,
  input  \时钟 ,
  output [31:0] Result
);

  // Probe on \数列初始值 
  // Probe on \数列初始值 
  // Probe on \等差值 
  // Probe on \等差值 
  // Probe on Result
  // Probe on Result

  // Other names for the same wires on the sheet: 数列初值[31:0] = \数列初始值 ; 累加和[31:0] = Result

  // Notes on the sheet:
  //   不要改变此引脚区域内容，也不要改变ALU封装形式
  //   请在下方利用上方输入输出引脚的隧道信号构建等差数列求和电路，ctrl+d复制选择部件
  //   华中科技大学计算机学院 计算机组成原理，鸣谢加州大学伯克利CS61C课程
  //   输出引脚
  //   探测区域
endmodule

module Carry_74182 (
  input  C0,
  input  [3:0] G,
  input  [3:0] P,
  output C4,
  output C3,
  output C2,
  output C1,
  output P4S,
  output G4S
);

  wire and_1_out, and_2_out, and_3_out, and_4_out, and_5_out, and_6_out, and_7_out, and_8_out, and_9_out,
       and_10_out;

  and and_1 (and_1_out, G[2], P[3]);
  and and_2 (and_2_out, G[1], P[3], P[2]);
  or or_1 (C4, G[3], and_1_out, and_2_out, and_3_out, and_4_out);
  and and_3 (and_3_out, G[0], P[3], P[2], P[1]);
  and and_4 (and_4_out, C0, P[3], P[2], P[1], P[0]);
  and and_5 (and_5_out, G[1], P[2]);
  or or_2 (C3, G[2], and_5_out, and_6_out, and_7_out);
  and and_6 (and_6_out, G[0], P[2], P[1]);
  and and_7 (and_7_out, C0, P[2], P[1], P[0]);
  GroupCarry groupcarry_1 (.G4S(G4S), .P4S(P4S), .G(G), .P(P));
  or or_3 (C2, G[1], and_8_out, and_9_out);
  and and_8 (and_8_out, G[0], P[1]);
  and and_9 (and_9_out, C0, P[1], P[0]);
  or or_4 (C1, G[0], and_10_out);
  and and_10 (and_10_out, C0, P[0]);
endmodule

module GPG (
  input  [3:0] Y,
  input  [3:0] X,
  output [3:0] G,
  output [3:0] P
);

  and and_1 (G[3], X[3], Y[3]);
  and and_2 (G[2], X[2], Y[2]);
  xor xor_1 (P[3], X[3], Y[3]);
  xor xor_2 (P[2], X[2], Y[2]);
  and and_3 (G[1], X[1], Y[1]);
  xor xor_3 (P[1], X[1], Y[1]);
  and and_4 (G[0], X[0], Y[0]);
  xor xor_4 (P[0], X[0], Y[0]);
endmodule

module Adder4_74181 (
  input  C0,
  input  [3:0] X,
  input  [3:0] Y,
  output G4S,
  output P4S,
  output C4,
  output [3:0] S
);

  wire carry_74182_1_c1, carry_74182_1_c2, carry_74182_1_c3;
  wire [3:0] gpg_1_g, gpg_1_p;

  xor xor_1 (S[3], gpg_1_p[3], carry_74182_1_c3);
  xor xor_2 (S[2], gpg_1_p[2], carry_74182_1_c2);
  xor xor_3 (S[1], gpg_1_p[1], carry_74182_1_c1);
  Carry_74182 carry_74182_1 (
    .C4(C4), .C3(carry_74182_1_c3), .C2(carry_74182_1_c2), .C1(carry_74182_1_c1), .G(gpg_1_g), .P4S(P4S),
    .G4S(G4S), .P(gpg_1_p), .C0(C0));
  GPG gpg_1 (.G(gpg_1_g), .X(X), .Y(Y), .P(gpg_1_p));
  xor xor_4 (S[0], gpg_1_p[0], C0);
endmodule

module GroupCarry (
  input  [3:0] G,
  input  [3:0] P,
  output G4S,
  output P4S
);

  wire and_1_out, and_2_out, and_3_out;

  and and_1 (and_1_out, P[3], G[2]);
  or or_1 (G4S, G[3], and_1_out, and_2_out, and_3_out);
  and and_2 (and_2_out, P[3], P[2], G[1]);
  and and_3 (and_3_out, P[3], P[2], P[1], G[0]);
  and and_4 (P4S, P[3], P[2], P[1], P[0]);
endmodule

module Adder32 (
  input  C0,
  input  [31:0] X,
  input  [31:0] Y,
  output Cout,
  output [31:0] S
);

  wire carry_74182_1_c1, carry_74182_1_c3;
  wire [3:0] adder16_4_gs, adder16_4_ps;

  Adder16 adder16_1 (
    .GS(adder16_4_gs[3]), .PS(adder16_4_ps[3]), .X({16{1'b0}}), .Y({16{1'b0}}), .C0(carry_74182_1_c3));  // open: Cout, S
  Adder16 adder16_2 (
    .GS(adder16_4_gs[2]), .PS(adder16_4_ps[2]), .X({16{1'b0}}), .Y({16{1'b0}}), .C0(Cout));  // open: Cout, S
  Carry_74182 carry_74182_1 (
    .C3(carry_74182_1_c3), .C2(Cout), .C1(carry_74182_1_c1), .G(adder16_4_gs), .P(adder16_4_ps), .C0(C0));  // open: C4, P4S, G4S
  Adder16 adder16_3 (
    .GS(adder16_4_gs[1]), .PS(adder16_4_ps[1]), .S(S[31:16]), .X(X[31:16]), .Y(Y[31:16]),
    .C0(carry_74182_1_c1));  // open: Cout
  Adder16 adder16_4 (
    .GS(adder16_4_gs[0]), .PS(adder16_4_ps[0]), .S(S[15:0]), .X(X[15:0]), .Y(Y[15:0]), .C0(C0));  // open: Cout
endmodule

module Adder16 (
  input  C0,
  input  [15:0] X,
  input  [15:0] Y,
  output GS,
  output PS,
  output Cout,
  output [15:0] S
);

  wire carry_74182_1_c1, carry_74182_1_c2, carry_74182_1_c3;
  wire [3:0] adder4_74181_4_g4s, adder4_74181_4_p4s;

  Adder4_74181 adder4_74181_1 (
    .G4S(adder4_74181_4_g4s[3]), .P4S(adder4_74181_4_p4s[3]), .S(S[15:12]), .X(X[15:12]), .Y(Y[15:12]),
    .C0(carry_74182_1_c3));  // open: C4
  Adder4_74181 adder4_74181_2 (
    .G4S(adder4_74181_4_g4s[2]), .P4S(adder4_74181_4_p4s[2]), .S(S[11:8]), .X(X[11:8]), .Y(Y[11:8]),
    .C0(carry_74182_1_c2));  // open: C4
  Carry_74182 carry_74182_1 (
    .C4(Cout), .C3(carry_74182_1_c3), .C2(carry_74182_1_c2), .C1(carry_74182_1_c1), .G(adder4_74181_4_g4s),
    .P4S(PS), .G4S(GS), .P(adder4_74181_4_p4s), .C0(C0));
  Adder4_74181 adder4_74181_3 (
    .G4S(adder4_74181_4_g4s[1]), .P4S(adder4_74181_4_p4s[1]), .S(S[7:4]), .X(X[7:4]), .Y(Y[7:4]),
    .C0(carry_74182_1_c1));  // open: C4
  Adder4_74181 adder4_74181_4 (
    .G4S(adder4_74181_4_g4s[0]), .P4S(adder4_74181_4_p4s[0]), .S(S[3:0]), .X(X[3:0]), .Y(Y[3:0]), .C0(C0));  // open: C4
endmodule
