// Logisim project regfile-test.circ as structural Verilog: 1 circuit, main circuit main
module main (
  output [7:0] test_num,
  output [31:0] Reg_0_Value,
  output [31:0] Reg_1_Value,
  output [31:0] Reg_2_Value,
  output [31:0] Reg_3_Value,
  output [31:0] Read_Data_1,
  output [31:0] Read_Data_2
);

  wire clock_1_out;
  wire [7:0] adder_1_out;
  wire [15:0] rom_2_data;
  wire [31:0] WriteData;

  Register register_1 (.D(adder_1_out), .en(1'b1), .Q(test_num), .clk(clock_1_out));  // open: clr
  Adder adder_1 (.a(8'h1), .b(test_num), .out(adder_1_out));  // open: cin, cout
  ROM #(.dataWidth(32)) rom_1 (.addr(test_num), .data(WriteData));  // open: sel
  ROM #(.dataWidth(16)) rom_2 (.addr(test_num), .data(rom_2_data), .sel(1'b1));
  Clock clock_1 (.out(clock_1_out));
  regfile_main main_1 (
    .Reg1_num(rom_2_data[4:0]), .Reg2(rom_2_data[9:5]), .Write_Reg_num(rom_2_data[14:10]), .Din(WriteData),
    .Write_Enable(rom_2_data[15]), .Clock(clock_1_out), .Reg1(Read_Data_1), .Reg2_2(Read_Data_2),
    .s0_Value(Reg_0_Value), .s1_Value(Reg_1_Value), .s2_Value(Reg_2_Value), .ra_Value(Reg_3_Value));

  // Notes on the sheet:
  //   contents of rom_1 (hex, n*v repeats v):
  //   49823094 432324 4324 21321 31212 f 2121af 343e
  //   图中不应该有蓝色或红色线缆，也不应该出现未知状态 x.
  //   你的寄存器文件封装正好合适放在这里
endmodule
