// Logisim project CS1409_U201414800_刘一龙_cpu.circ as structural Verilog: 7 circuits, main circuit MIPS
module MIPS (
);

  wire ALUSham, ALUSrc, and_3_out, Beq, Bne, clk, clock_1_out, cnt1_1_value, comparator_1_eq,
       controlunit_1_alutype, controlunit_1_branchtype, controlunit_1_jmptype, controlunit_1_memtype,
       controlunit_1_othertype, counter_1_q, Eq, ExtOp, Halt, Jal, Jmp, Jr, not_1_out, not_2_out, RAMtoReg,
       RAMWe, RegDst, register_1_q, RegWe, Syscall;
  wire [3:0] ALUOp, multiplexer_11_out_2, multiplexer_11_out_3, multiplexer_11_out_4, multiplexer_11_out_5;
  wire [4:0] multiplexer_1_out, multiplexer_2_out, multiplexer_3_out, multiplexer_4_out, rd, rs, rt, sham;
  wire [5:0] functy, op;
  wire [15:0] imm16, multiplexer_11_out;
  wire [25:0] imm26;
  wire [31:0] a0, alu_1_result, bit_extender_1_out, bit_extender_2_out, bit_extender_3_out, counter_2_value,
       counter_3_value, counter_4_value, counter_5_value, counter_6_value, counter_7_value, instruction,
       main_1_reg1, main_1_reg2_2, multiplexer_5_out, multiplexer_6_out, multiplexer_7_out,
       multiplexer_8_out, multiplexer_9_out, multiplexer_10_out, PC, ra, ram_1_data, s0, s1, s2;

  Clock clock_1 (.out(clock_1_out));
  Counter_part #(.width(1), .max('h1), .ongoal("stay")) counter_1 (
    .load(1'b0), .count(1'b1), .Q(counter_1_q), .clk(Halt), .clr(1'b0));  // open: D, carry
  // Probe on ALUOp
  // Probe on op
  // Probe on rs
  // Probe on rt
  // Probe on rd
  // Probe on sham
  // Probe on functy
  // Probe on imm16
  // Probe on imm26
  and and_1 (clk, clock_1_out, not_1_out);
  not not_1 (not_1_out, cnt1_1_value);
  Cnt1 cnt1_1 (.enable(counter_1_q), .clk(clk), .value(cnt1_1_value));
  // Probe on s0
  // Probe on s1
  Multiplexer #(.width(5), .enable("false")) multiplexer_1 (.in0(rs), .in1(rt), .out(multiplexer_1_out), .sel(ALUSham));
  Multiplexer #(.width(5), .enable("false")) multiplexer_2 (
    .in0(rt), .in1(5'b00010), .out(multiplexer_2_out), .sel(Syscall));
  Multiplexer #(.width(5), .enable("false")) multiplexer_3 (.in0(rt), .in1(rd), .out(multiplexer_3_out), .sel(RegDst));
  Multiplexer #(.width(5), .enable("false")) multiplexer_4 (
    .in0(multiplexer_3_out), .in1({5{1'b1}}), .out(multiplexer_4_out), .sel(Jal));
  IFU ifu_1 (
    .clk(clk), .instruction(instruction), .Beq(Beq), .Bne(Bne), .Eq(Eq), .Jmp(Jmp), .Jr(Jr),
    .target(main_1_reg1), .PC(PC), .Jal(Jal));
  // Probe on s2
  Decoder decoder_1 (
    .instruction(instruction), .op(op), .rs(rs), .rt(rt), .rd(rd), .sham(sham), .funct(functy),
    .imm16(imm16), .imm26(imm26));
  // Probe on ra
  \CS1409_U201414800_刘一龙_regfile_main  main_1 (
    .Reg1_num(multiplexer_1_out), .Reg2(multiplexer_2_out), .Write_Reg_num(multiplexer_4_out),
    .Din(multiplexer_10_out), .Write_Enable(RegWe), .Clock(clk), .Reg1(main_1_reg1), .Reg2_2(main_1_reg2_2),
    .s0_Value(s0), .s1_Value(s1), .s2_Value(s2), .ra_Value(ra), .a0(a0));
  // Probe on PC
  assign bit_extender_1_out = {{16{1'b0}}, imm16};  // Bit_Extender bit_extender_1
  assign bit_extender_2_out = {{16{imm16[15]}}, imm16};  // Bit_Extender bit_extender_2
  // Probe on instruction
  Multiplexer #(.width(32), .enable("false")) multiplexer_5 (
    .in0(main_1_reg1), .in1(PC), .out(multiplexer_5_out), .sel(Jal));
  // Probe on bit_extender_1_out
  Multiplexer #(.width(32), .enable("false")) multiplexer_6 (
    .in0(bit_extender_1_out), .in1(bit_extender_2_out), .out(multiplexer_6_out), .sel(ExtOp));
  // Probe on counter_2_value
  Counter counter_2 (.enable(controlunit_1_alutype), .clk(clk), .value(counter_2_value));
  Multiplexer #(.width(32), .enable("false")) multiplexer_7 (
    .in0(main_1_reg2_2), .in1(multiplexer_6_out), .out(multiplexer_7_out), .sel(ALUSrc));
  // Probe on counter_3_value
  Counter counter_3 (.enable(controlunit_1_memtype), .clk(clk), .value(counter_3_value));
  Counter counter_4 (.enable(controlunit_1_jmptype), .clk(clk), .value(counter_4_value));
  // Probe on counter_4_value
  Counter counter_5 (.enable(controlunit_1_branchtype), .clk(clk), .value(counter_5_value));
  Multiplexer #(.width(32), .enable("false")) multiplexer_8 (
    .in0(multiplexer_7_out), .in1(bit_extender_3_out), .out(multiplexer_8_out), .sel(ALUSham));
  assign bit_extender_3_out = {{27{1'b0}}, sham};  // Bit_Extender bit_extender_3
  // Probe on counter_5_value
  // Probe on counter_6_value
  Counter counter_6 (.enable(controlunit_1_othertype), .clk(clk), .value(counter_6_value));
  ControlUnit controlunit_1 (
    .op(op), .funct(functy), .ALUOp(ALUOp), .RegWe(RegWe), .ALUSrc(ALUSrc), .RegDst(RegDst), .ExtOp(ExtOp),
    .ALUSham(ALUSham), .RAMtoReg(RAMtoReg), .RAMWe(RAMWe), .Beq(Beq), .Bne(Bne), .Jmp(Jmp), .Jr(Jr),
    .Jal(Jal), .Syscall(Syscall), .ALUType(controlunit_1_alutype), .MemType(controlunit_1_memtype),
    .JmpType(controlunit_1_jmptype), .BranchType(controlunit_1_branchtype),
    .OtherType(controlunit_1_othertype));
  Multiplexer #(.width(32), .enable("false")) multiplexer_9 (
    .in0(multiplexer_8_out), .in1(32'h4), .out(multiplexer_9_out), .sel(Jal));
  // Probe on counter_7_value
  Counter counter_7 (.enable(1'b1), .clk(clk), .value(counter_7_value));
  Multiplexer #(.width(32), .enable("false")) multiplexer_10 (
    .in0(alu_1_result), .in1(ram_1_data), .out(multiplexer_10_out), .sel(RAMtoReg));
  ALU alu_1 (
    .AluOP(ALUOp), .X(multiplexer_5_out), .Equal(Eq), .Result(alu_1_result), .Y(multiplexer_9_out));  // open: Signed_Overflow, Result_2, UnSigned_Overflow
  Comparator #(.width(32), .mode("unsigned")) comparator_1 (
    .a(32'ha), .b(main_1_reg2_2), .eq(comparator_1_eq));  // open: gt, lt
  Hex_Digit_Display hex_digit_display_1 (.value(multiplexer_11_out_5));  // open: dp
  and and_2 (Halt, comparator_1_eq, Syscall);
  Hex_Digit_Display hex_digit_display_2 (.value(multiplexer_11_out_3));  // open: dp
  Hex_Digit_Display hex_digit_display_3 (.value(multiplexer_11_out_4));  // open: dp
  and and_3 (and_3_out, not_2_out, Syscall);
  not not_2 (not_2_out, comparator_1_eq);
  RAM #(.addrWidth(24), .dataWidth(32), .bus("separate")) ram_1 (
    .addr(alu_1_result[25:2]), .din(main_1_reg2_2), .data(ram_1_data), .str(RAMWe), .sel(1'b1), .clk(clk),
    .ld(1'b1), .clr(1'b0));
  Hex_Digit_Display hex_digit_display_4 (.value(multiplexer_11_out[15:12]));  // open: dp
  Hex_Digit_Display hex_digit_display_5 (.value(multiplexer_11_out_2));  // open: dp
  Multiplexer #(.width(32), .enable("false")) multiplexer_11 (
    .in0({32{1'b0}}), .in1(a0),
    .out({multiplexer_11_out_5, multiplexer_11_out_4, multiplexer_11_out_3, multiplexer_11_out_2, multiplexer_11_out}),
    .sel(register_1_q));
  Register #(.width(1)) register_1 (.D(1'b1), .en(and_3_out), .Q(register_1_q), .clk(clk));  // open: clr
  Hex_Digit_Display hex_digit_display_6 (.value(multiplexer_11_out[7:4]));  // open: dp
  Hex_Digit_Display hex_digit_display_7 (.value(multiplexer_11_out[11:8]));  // open: dp
  Hex_Digit_Display hex_digit_display_8 (.value(multiplexer_11_out[3:0]));  // open: dp

  // Notes on the sheet:
  //   Syscall
  //   听说黑底绿字更好看
endmodule

module IFU (
  input  [31:0] target,
  input  Bne,
  input  Jr,
  input  Eq,
  input  Beq,
  input  Jmp,
  input  Jal,
  input  clk,
  output [31:0] instruction,
  output [31:0] PC
);

  wire and_1_out, and_2_out, not_1_out, or_1_out, or_2_out;
  wire [31:0] adder_1_out, adder_2_out, bit_extender_1_out, bit_extender_2_out, multiplexer_1_out,
       multiplexer_2_out, multiplexer_3_out, shifter_1_out, shifter_2_out;

  Register #(.width(32)) u_PC (.D(multiplexer_3_out), .en(1'b1), .Q(PC), .clk(clk), .clr(1'b0));
  Adder #(.width(32)) adder_1 (.a(32'h4), .b(PC), .out(adder_1_out), .cin(1'b0));  // open: cout
  and and_1 (and_1_out, Bne, not_1_out);
  not not_1 (not_1_out, Eq);
  and and_2 (and_2_out, Beq, Eq);
  ROM #(.addrWidth(10), .dataWidth(32)) rom_1 (.addr(PC[11:2]), .data(instruction), .sel(1'b1));
  or or_1 (or_1_out, and_1_out, and_2_out);
  assign bit_extender_1_out = {{16{instruction[15]}}, instruction[15:0]};  // Bit_Extender bit_extender_1
  Adder #(.width(32)) adder_2 (.a(adder_1_out), .b(shifter_1_out), .out(adder_2_out), .cin(1'b0));  // open: cout
  Shifter #(.width(32)) shifter_1 (.in(bit_extender_1_out), .\dist (5'b00010), .out(shifter_1_out));
  assign bit_extender_2_out = {{6{instruction[25]}}, instruction[25:0]};  // Bit_Extender bit_extender_2
  Shifter #(.width(32)) shifter_2 (.in(bit_extender_2_out), .\dist (5'b00010), .out(shifter_2_out));
  Multiplexer #(.width(32), .enable("false")) multiplexer_1 (
    .in0(adder_2_out), .in1({PC[31:28], shifter_2_out[27:0]}), .out(multiplexer_1_out), .sel(or_2_out));
  or or_2 (or_2_out, Jmp, Jal);
  Multiplexer #(.width(32), .enable("false")) multiplexer_2 (
    .in0(multiplexer_1_out), .in1(target), .out(multiplexer_2_out), .sel(Jr));
  Multiplexer #(.width(32), .enable("false")) multiplexer_3 (
    .in0(adder_1_out), .in1(multiplexer_2_out), .out(multiplexer_3_out), .sel(or_1_out));

  // Notes on the sheet:
  //   /4:word => byte
  //   contents of rom_1 (hex, n*v repeats v):
  //   20110001 8000c05 20110001 20120002 20130003 8000c09 20110001 20120002 20130003 8000c0d 20110001
  //   20120002 20130003 8000c11 20110001 20120002 20130003 c000cb8 20100001 20110001 118fc0 112020
  //   20020022 c 118882 12200001 8000c15 112020 20020022 c 20110001 118880 112020 20020022 c 12200001
  //   8000c1f 20110001 118fc0 112020 20020022 c 1188c3 112020 20020022 c 118903 112020 20020022 c 118903
  //   112020 20020022 c 118903 112020 20020022 c 118903 112020 20020022 c 118903 112020 20020022 c 118903
  //   112020 20020022 c 118903 112020 20020022 c 20100001 109fc0 139fc3 8021 2012000c 24160003 26100001
  //   3210000f 20080008 20090001 139900 2709825 132020 20020022 c 1094022 1500fff9 22100001 2018000f
  //   2188024 108700 20080008 20090001 139902 2709825 132021 20020022 c 1094022 1500fff9 108702 2c9b022
  //   12c00001 8000c50 4020 1084027 84400 3508ffff 82021 20020022 c 2010ffff 20110000 ae300000 22100001
  //   22310004 ae300000 22100001 22310004 ae300000 22100001 22310004 ae300000 22100001 22310004 ae300000
  //   22100001 22310004 ae300000 22100001 22310004 ae300000 22100001 22310004 ae300000 22100001 22310004
  //   ae300000 22100001 22310004 ae300000 22100001 22310004 ae300000 22100001 22310004 ae300000 22100001
  //   22310004 ae300000 22100001 22310004 ae300000 22100001 22310004 ae300000 22100001 22310004 ae300000
  //   22100001 22310004 22100001 8020 2011003c 8e130000 8e340000 274402a 11000002 ae330000 ae140000
  //   2231fffc 1611fff8 102020 20020022 c 22100004 2011003c 1611fff2 2002000a c 20100000 22100001 102020
  //   20020022 c 22100002 102020 20020022 c 22100003 102020 20020022 c 22100004 102020 20020022 c 22100005
  //   102020 20020022 c 22100006 102020 20020022 c 22100007 102020 20020022 c 22100008 102020 20020022
  //   20020022 c 3e00008
  //   PC = PC + 4 + Offset * 4
  //   PC = PC_high_4||addr||00
endmodule

module Decoder (
  input  [31:0] instruction,
  output [25:0] imm26,
  output [15:0] imm16,
  output [5:0] op,
  output [4:0] rs,
  output [4:0] rt,
  output [4:0] rd,
  output [4:0] sham,
  output [5:0] funct
);


  assign funct = instruction[5:0];
  assign imm16 = instruction[15:0];
  assign imm26 = instruction[25:0];
  assign op = instruction[31:26];
  assign rd = instruction[15:11];
  assign rs = instruction[25:21];
  assign rt = instruction[20:16];
  assign sham = instruction[10:6];

  // Notes on the sheet:
  //   R 型指令译码
  //   I 型指令译码
  //   J 型指令译码
endmodule

module InstructionTyper (
  input  [5:0] op,
  input  [5:0] functy,
  output ADD,
  output ADDI,
  output ADDIU,
  output ADDU,
  output AND,
  output ANDI,
  output SLL,
  output SRA,
  output SRL,
  output SUB,
  output OR,
  output ORI,
  output NOR,
  output LW,
  output SW,
  output BEQ,
  output BNE,
  output SLT,
  output SLTI,
  output SLTU,
  output JMP,
  output JAL,
  output JR,
  output SYSCALL
);

  wire not_1_out, not_2_out, not_3_out, not_4_out, not_5_out, not_6_out, not_7_out, not_8_out, not_9_out,
       not_10_out, not_11_out, not_12_out, not_13_out, not_14_out, not_15_out, not_16_out, not_17_out,
       not_18_out, not_19_out, not_20_out, not_21_out, not_22_out, not_23_out, not_24_out, not_25_out,
       not_26_out, not_27_out, not_28_out, not_29_out, not_30_out, not_31_out, not_32_out, not_33_out,
       not_34_out, not_35_out, not_36_out, not_37_out, not_38_out, not_39_out, not_40_out, not_41_out,
       not_42_out, not_43_out, not_44_out, not_45_out, not_46_out, not_47_out, not_48_out, not_49_out,
       not_50_out, not_51_out, not_52_out, not_53_out, not_54_out, not_55_out, not_56_out, not_57_out,
       not_58_out, not_59_out, not_60_out, not_61_out, not_62_out, not_63_out, not_64_out, not_65_out,
       not_66_out, not_67_out, not_68_out, not_69_out, not_70_out, not_71_out, not_72_out, not_73_out,
       not_74_out, not_75_out, not_76_out, not_77_out, not_78_out, not_79_out, not_80_out, not_81_out,
       not_82_out, not_83_out, not_84_out, not_85_out, not_86_out, not_87_out, not_88_out, not_89_out,
       not_90_out, not_91_out, not_92_out, not_93_out, not_94_out, not_95_out, not_96_out, not_97_out,
       not_98_out, not_99_out, not_100_out, not_101_out, not_102_out, not_103_out, not_104_out, not_105_out,
       not_106_out, not_107_out, not_108_out, not_109_out, not_110_out, not_111_out, not_112_out,
       not_113_out, not_114_out, not_115_out, not_116_out, not_117_out, not_118_out, not_119_out,
       not_120_out, not_121_out, not_122_out, not_123_out, not_124_out, not_125_out, not_126_out,
       not_127_out, not_128_out, not_129_out, not_130_out, not_131_out, not_132_out, not_133_out,
       not_134_out, not_135_out, not_136_out, not_137_out, not_138_out, not_139_out, not_140_out,
       not_141_out, not_142_out, not_143_out, not_144_out, not_145_out, not_146_out, not_147_out,
       not_148_out, not_149_out, not_150_out, not_151_out, not_152_out, not_153_out, not_154_out,
       not_155_out, not_156_out, not_157_out, not_158_out, not_159_out, not_160_out, not_161_out,
       not_162_out, not_163_out, not_164_out, not_165_out, not_166_out, not_167_out, not_168_out,
       not_169_out, not_170_out, not_171_out, not_172_out;

  not not_1 (not_1_out, op[5]);
  not not_2 (not_2_out, op[4]);
  not not_3 (not_3_out, op[3]);
  not not_4 (not_4_out, op[2]);
  not not_5 (not_5_out, op[1]);
  not not_6 (not_6_out, op[0]);
  not not_7 (not_7_out, functy[4]);
  not not_8 (not_8_out, functy[3]);
  not not_9 (not_9_out, functy[2]);
  not not_10 (not_10_out, functy[1]);
  not not_11 (not_11_out, functy[0]);
  not not_12 (not_12_out, op[5]);
  not not_13 (not_13_out, op[4]);
  not not_14 (not_14_out, op[2]);
  not not_15 (not_15_out, op[1]);
  not not_16 (not_16_out, op[0]);
  not not_17 (not_17_out, op[5]);
  not not_18 (not_18_out, op[4]);
  not not_19 (not_19_out, op[2]);
  not not_20 (not_20_out, op[1]);
  not not_21 (not_21_out, op[5]);
  not not_22 (not_22_out, op[4]);
  not not_23 (not_23_out, op[3]);
  not not_24 (not_24_out, op[2]);
  not not_25 (not_25_out, op[1]);
  not not_26 (not_26_out, op[0]);
  not not_27 (not_27_out, functy[4]);
  not not_28 (not_28_out, functy[3]);
  not not_29 (not_29_out, functy[2]);
  not not_30 (not_30_out, functy[1]);
  not not_31 (not_31_out, op[5]);
  not not_32 (not_32_out, op[4]);
  not not_33 (not_33_out, op[3]);
  not not_34 (not_34_out, op[2]);
  not not_35 (not_35_out, op[1]);
  not not_36 (not_36_out, op[0]);
  not not_37 (not_37_out, functy[4]);
  not not_38 (not_38_out, functy[3]);
  not not_39 (not_39_out, functy[1]);
  not not_40 (not_40_out, functy[0]);
  not not_41 (not_41_out, op[5]);
  not not_42 (not_42_out, op[4]);
  not not_43 (not_43_out, op[1]);
  not not_44 (not_44_out, op[0]);
  not not_45 (not_45_out, op[5]);
  not not_46 (not_46_out, op[4]);
  not not_47 (not_47_out, op[3]);
  not not_48 (not_48_out, op[2]);
  not not_49 (not_49_out, op[1]);
  not not_50 (not_50_out, op[0]);
  not not_51 (not_51_out, functy[5]);
  not not_52 (not_52_out, functy[4]);
  not not_53 (not_53_out, functy[3]);
  not not_54 (not_54_out, functy[2]);
  not not_55 (not_55_out, functy[1]);
  not not_56 (not_56_out, functy[0]);
  not not_57 (not_57_out, op[5]);
  not not_58 (not_58_out, op[4]);
  not not_59 (not_59_out, op[3]);
  not not_60 (not_60_out, op[2]);
  not not_61 (not_61_out, op[1]);
  not not_62 (not_62_out, op[0]);
  not not_63 (not_63_out, functy[5]);
  not not_64 (not_64_out, functy[4]);
  not not_65 (not_65_out, functy[3]);
  not not_66 (not_66_out, functy[2]);
  not not_67 (not_67_out, op[5]);
  not not_68 (not_68_out, op[4]);
  not not_69 (not_69_out, op[3]);
  not not_70 (not_70_out, op[2]);
  not not_71 (not_71_out, op[1]);
  not not_72 (not_72_out, op[0]);
  not not_73 (not_73_out, functy[5]);
  not not_74 (not_74_out, functy[4]);
  not not_75 (not_75_out, functy[3]);
  not not_76 (not_76_out, functy[2]);
  not not_77 (not_77_out, functy[0]);
  not not_78 (not_78_out, op[5]);
  not not_79 (not_79_out, op[4]);
  not not_80 (not_80_out, op[3]);
  not not_81 (not_81_out, op[2]);
  not not_82 (not_82_out, op[1]);
  not not_83 (not_83_out, op[0]);
  not not_84 (not_84_out, functy[4]);
  not not_85 (not_85_out, functy[3]);
  not not_86 (not_86_out, functy[2]);
  not not_87 (not_87_out, functy[0]);
  not not_88 (not_88_out, op[5]);
  not not_89 (not_89_out, op[4]);
  not not_90 (not_90_out, op[3]);
  not not_91 (not_91_out, op[2]);
  not not_92 (not_92_out, op[1]);
  not not_93 (not_93_out, op[0]);
  not not_94 (not_94_out, functy[4]);
  not not_95 (not_95_out, functy[3]);
  not not_96 (not_96_out, functy[1]);
  not not_97 (not_97_out, op[5]);
  not not_98 (not_98_out, op[4]);
  not not_99 (not_99_out, op[1]);
  not not_100 (not_100_out, op[5]);
  not not_101 (not_101_out, op[4]);
  not not_102 (not_102_out, op[3]);
  not not_103 (not_103_out, op[2]);
  not not_104 (not_104_out, op[1]);
  not not_105 (not_105_out, op[0]);
  not not_106 (not_106_out, functy[4]);
  not not_107 (not_107_out, functy[3]);
  not not_108 (not_108_out, op[4]);
  not not_109 (not_109_out, op[3]);
  not not_110 (not_110_out, op[2]);
  not not_111 (not_111_out, op[4]);
  not not_112 (not_112_out, op[2]);
  not not_113 (not_113_out, op[5]);
  not not_114 (not_114_out, op[4]);
  not not_115 (not_115_out, op[3]);
  not not_116 (not_116_out, op[1]);
  not not_117 (not_117_out, op[0]);
  not not_118 (not_118_out, op[5]);
  not not_119 (not_119_out, op[4]);
  not not_120 (not_120_out, op[3]);
  not not_121 (not_121_out, op[1]);
  not not_122 (not_122_out, op[5]);
  not not_123 (not_123_out, op[4]);
  not not_124 (not_124_out, op[3]);
  not not_125 (not_125_out, op[2]);
  not not_126 (not_126_out, op[1]);
  not not_127 (not_127_out, op[0]);
  not not_128 (not_128_out, functy[4]);
  not not_129 (not_129_out, functy[2]);
  not not_130 (not_130_out, functy[0]);
  not not_131 (not_131_out, op[5]);
  not not_132 (not_132_out, op[4]);
  not not_133 (not_133_out, op[2]);
  not not_134 (not_134_out, op[0]);
  not not_135 (not_135_out, op[5]);
  not not_136 (not_136_out, op[4]);
  not not_137 (not_137_out, op[3]);
  not not_138 (not_138_out, op[2]);
  not not_139 (not_139_out, op[1]);
  not not_140 (not_140_out, op[0]);
  not not_141 (not_141_out, functy[4]);
  not not_142 (not_142_out, functy[2]);
  not not_143 (not_143_out, op[5]);
  not not_144 (not_144_out, op[4]);
  not not_145 (not_145_out, op[3]);
  not not_146 (not_146_out, op[2]);
  not not_147 (not_147_out, op[0]);
  not not_148 (not_148_out, op[5]);
  not not_149 (not_149_out, op[4]);
  not not_150 (not_150_out, op[3]);
  not not_151 (not_151_out, op[2]);
  not not_152 (not_152_out, op[5]);
  not not_153 (not_153_out, op[4]);
  not not_154 (not_154_out, op[3]);
  not not_155 (not_155_out, op[2]);
  not not_156 (not_156_out, op[1]);
  not not_157 (not_157_out, op[0]);
  not not_158 (not_158_out, functy[5]);
  not not_159 (not_159_out, functy[4]);
  not not_160 (not_160_out, functy[2]);
  not not_161 (not_161_out, functy[1]);
  not not_162 (not_162_out, functy[0]);
  not not_163 (not_163_out, op[5]);
  not not_164 (not_164_out, op[4]);
  not not_165 (not_165_out, op[3]);
  not not_166 (not_166_out, op[2]);
  not not_167 (not_167_out, op[1]);
  not not_168 (not_168_out, op[0]);
  not not_169 (not_169_out, functy[5]);
  not not_170 (not_170_out, functy[4]);
  not not_171 (not_171_out, functy[1]);
  not not_172 (not_172_out, functy[0]);
  and and_1 (ADD, not_1_out, not_2_out, not_3_out, not_4_out, not_5_out, not_6_out, functy[5], not_7_out, not_8_out, not_9_out, not_10_out, not_11_out);
  and and_2 (ADDI, not_12_out, not_13_out, op[3], not_14_out, not_15_out, not_16_out);
  and and_3 (ADDIU, not_17_out, not_18_out, op[3], not_19_out, not_20_out, op[0]);
  and and_4 (ADDU, not_21_out, not_22_out, not_23_out, not_24_out, not_25_out, not_26_out, functy[5], not_27_out, not_28_out, not_29_out, not_30_out, functy[0]);
  and and_5 (AND, not_31_out, not_32_out, not_33_out, not_34_out, not_35_out, not_36_out, functy[5], not_37_out, not_38_out, functy[2], not_39_out, not_40_out);
  and and_6 (ANDI, not_41_out, not_42_out, op[3], op[2], not_43_out, not_44_out);
  and and_7 (SLL, not_45_out, not_46_out, not_47_out, not_48_out, not_49_out, not_50_out, not_51_out, not_52_out, not_53_out, not_54_out, not_55_out, not_56_out);
  and and_8 (SRA, not_57_out, not_58_out, not_59_out, not_60_out, not_61_out, not_62_out, not_63_out, not_64_out, not_65_out, not_66_out, functy[1], functy[0]);
  and and_9 (SRL, not_67_out, not_68_out, not_69_out, not_70_out, not_71_out, not_72_out, not_73_out, not_74_out, not_75_out, not_76_out, functy[1], not_77_out);
  and and_10 (SUB, not_78_out, not_79_out, not_80_out, not_81_out, not_82_out, not_83_out, functy[5], not_84_out, not_85_out, not_86_out, functy[1], not_87_out);
  and and_11 (OR, not_88_out, not_89_out, not_90_out, not_91_out, not_92_out, not_93_out, functy[5], not_94_out, not_95_out, functy[2], not_96_out, functy[0]);
  and and_12 (ORI, not_97_out, not_98_out, op[3], op[2], not_99_out, op[0]);
  and and_13 (NOR, not_100_out, not_101_out, not_102_out, not_103_out, not_104_out, not_105_out, functy[5], not_106_out, not_107_out, functy[2], functy[1], functy[0]);
  and and_14 (LW, op[5], not_108_out, not_109_out, not_110_out, op[1], op[0]);
  and and_15 (SW, op[5], not_111_out, op[3], not_112_out, op[1], op[0]);
  and and_16 (BEQ, not_113_out, not_114_out, not_115_out, op[2], not_116_out, not_117_out);
  and and_17 (BNE, not_118_out, not_119_out, not_120_out, op[2], not_121_out, op[0]);
  and and_18 (SLT, not_122_out, not_123_out, not_124_out, not_125_out, not_126_out, not_127_out, functy[5], not_128_out, functy[3], not_129_out, functy[1], not_130_out);
  and and_19 (SLTI, not_131_out, not_132_out, op[3], not_133_out, op[1], not_134_out);
  and and_20 (SLTU, not_135_out, not_136_out, not_137_out, not_138_out, not_139_out, not_140_out, functy[5], not_141_out, functy[3], not_142_out, functy[1], functy[0]);
  and and_21 (JMP, not_143_out, not_144_out, not_145_out, not_146_out, op[1], not_147_out);
  and and_22 (JAL, not_148_out, not_149_out, not_150_out, not_151_out, op[1], op[0]);
  and and_23 (JR, not_152_out, not_153_out, not_154_out, not_155_out, not_156_out, not_157_out, not_158_out, not_159_out, functy[3], not_160_out, not_161_out, not_162_out);
  and and_24 (SYSCALL, not_163_out, not_164_out, not_165_out, not_166_out, not_167_out, not_168_out, not_169_out, not_170_out, functy[3], functy[2], not_171_out, not_172_out);

  // Other names for the same wires on the sheet: FU0 = functy[0]; FU1 = functy[1]; FU2 = functy[2]; FU3 = functy[3];
  //   FU4 = functy[4]; FU5 = functy[5]
endmodule

module ControlUnit (
  input  [5:0] op,
  input  [5:0] funct,
  output ALUType,
  output MemType,
  output JmpType,
  output BranchType,
  output OtherType,
  output [3:0] ALUOp,
  output RegWe,
  output ALUSrc,
  output RegDst,
  output ExtOp,
  output ALUSham,
  output RAMtoReg,
  output RAMWe,
  output Beq,
  output Bne,
  output Jmp,
  output Jal,
  output Jr,
  output Syscall
);

  wire instructiontyper_1_add, instructiontyper_1_addi, instructiontyper_1_addiu, instructiontyper_1_addu,
       instructiontyper_1_and, instructiontyper_1_andi, instructiontyper_1_beq, instructiontyper_1_bne,
       instructiontyper_1_nor, instructiontyper_1_or, instructiontyper_1_ori, instructiontyper_1_sll,
       instructiontyper_1_slt, instructiontyper_1_slti, instructiontyper_1_sltu, instructiontyper_1_sra,
       instructiontyper_1_srl, instructiontyper_1_sub;

  InstructionTyper instructiontyper_1 (
    .op(op), .functy(funct), .ADD(instructiontyper_1_add), .ADDI(instructiontyper_1_addi),
    .ADDIU(instructiontyper_1_addiu), .ADDU(instructiontyper_1_addu), .AND(instructiontyper_1_and),
    .ANDI(instructiontyper_1_andi), .SLL(instructiontyper_1_sll), .SRA(instructiontyper_1_sra),
    .SRL(instructiontyper_1_srl), .SUB(instructiontyper_1_sub), .OR(instructiontyper_1_or),
    .ORI(instructiontyper_1_ori), .NOR(instructiontyper_1_nor), .LW(RAMtoReg), .SW(RAMWe),
    .BEQ(instructiontyper_1_beq), .BNE(instructiontyper_1_bne), .SLT(instructiontyper_1_slt),
    .SLTI(instructiontyper_1_slti), .SLTU(instructiontyper_1_sltu), .JMP(Jmp), .JAL(Jal), .JR(Jr),
    .SYSCALL(Syscall));
  or u_ALUType (ALUType, instructiontyper_1_add, instructiontyper_1_addi, instructiontyper_1_addiu, instructiontyper_1_and, instructiontyper_1_andi, instructiontyper_1_sll, instructiontyper_1_sra, instructiontyper_1_srl, instructiontyper_1_sub, instructiontyper_1_or, instructiontyper_1_ori, instructiontyper_1_nor);
  or or_1 (ALUOp[0], instructiontyper_1_add, instructiontyper_1_addi, instructiontyper_1_addiu, instructiontyper_1_addu, instructiontyper_1_and, instructiontyper_1_andi, instructiontyper_1_sra, RAMtoReg, RAMWe, instructiontyper_1_slt, instructiontyper_1_slti, Jal);
  or u_MemType (MemType, RAMtoReg, RAMWe);
  or or_2 (ALUOp[1], instructiontyper_1_and, instructiontyper_1_andi, instructiontyper_1_srl, instructiontyper_1_sub, instructiontyper_1_nor, instructiontyper_1_slt, instructiontyper_1_slti);
  or or_3 (ALUOp[2], instructiontyper_1_add, instructiontyper_1_addi, instructiontyper_1_addiu, instructiontyper_1_addu, instructiontyper_1_and, instructiontyper_1_andi, instructiontyper_1_sub, RAMtoReg, RAMWe, instructiontyper_1_sltu, Jal);
  or u_JmpType (JmpType, Jmp, Jal, Jr);
  or or_4 (ALUOp[3], instructiontyper_1_or, instructiontyper_1_ori, instructiontyper_1_nor, instructiontyper_1_slt, instructiontyper_1_slti, instructiontyper_1_sltu);
  or u_BranchType (BranchType, instructiontyper_1_beq, instructiontyper_1_bne);
  or or_5 (RegWe, instructiontyper_1_add, instructiontyper_1_addi, instructiontyper_1_addiu, instructiontyper_1_addu, instructiontyper_1_and, instructiontyper_1_andi, instructiontyper_1_sll, instructiontyper_1_sra, instructiontyper_1_srl, instructiontyper_1_sub, instructiontyper_1_or, instructiontyper_1_ori, instructiontyper_1_nor, RAMtoReg, instructiontyper_1_slt, instructiontyper_1_slti, instructiontyper_1_sltu, Jal);
  or u_OtherType (OtherType, instructiontyper_1_slt, instructiontyper_1_slti, instructiontyper_1_addu, instructiontyper_1_sltu, Syscall);
  or or_6 (ALUSrc, instructiontyper_1_addi, instructiontyper_1_addiu, instructiontyper_1_andi, instructiontyper_1_ori, RAMtoReg, RAMWe, instructiontyper_1_slti);
  or or_7 (RegDst, instructiontyper_1_add, instructiontyper_1_addu, instructiontyper_1_and, instructiontyper_1_sll, instructiontyper_1_sra, instructiontyper_1_srl, instructiontyper_1_sub, instructiontyper_1_or, instructiontyper_1_nor, instructiontyper_1_slt, instructiontyper_1_sltu);
  or or_8 (ExtOp, instructiontyper_1_addi, instructiontyper_1_addiu, RAMtoReg, RAMWe, instructiontyper_1_slti);
  or or_9 (ALUSham, instructiontyper_1_sll, instructiontyper_1_sra, instructiontyper_1_srl);
  or or_10 (Beq, instructiontyper_1_beq, Jmp, Jal, Jr);
  or or_11 (Bne, instructiontyper_1_bne, Jmp, Jal, Jr);
endmodule

module Counter (
  input  enable,
  input  clk,
  output [31:0] value
);

  wire [31:0] adder_1_out;

  Register #(.width(32)) register_1 (.D(adder_1_out), .en(enable), .Q(value), .clk(clk));  // open: clr
  Adder #(.width(32)) adder_1 (.a(32'h1), .b(value), .out(adder_1_out));  // open: cin, cout
endmodule

module Cnt1 (
  input  enable,
  input  clk,
  output value
);

  wire adder_1_out;

  Register #(.width(1)) register_1 (.D(adder_1_out), .en(enable), .Q(value), .clk(clk));  // open: clr
  Adder #(.width(1)) adder_1 (.a(1'b1), .b(value), .out(adder_1_out));  // open: cin, cout
endmodule
