// Logisim project 74166.circ as structural Verilog: 1 circuit, main circuit 74166
module _74166 (
  input  D0,
  input  D1,
  input  D2,
  input  D3,
  input  D4,
  input  D5,
  input  D6,
  input  D7,
  input  nPE,
  input  DS,
  input  CP,
  input  nCE,
  input  nMR,
  output Q7,
  output [7:0] test
);

  wire and_1_out, and_2_out, and_3_out, and_4_out, and_5_out, and_6_out, and_7_out, and_8_out, and_9_out,
       and_10_out, and_11_out, and_12_out, and_13_out, and_14_out, and_15_out, and_16_out, buffer_1_out,
       buffer_2_out, buffer_3_out, buffer_4_out, buffer_5_out, buffer_6_out, buffer_7_out, buffer_8_out,
       buffer_9_out, buffer_10_out, buffer_11_out, nor_1_out, nor_2_out, nor_3_out, nor_4_out, nor_5_out,
       nor_6_out, nor_7_out, nor_8_out, nor_9_out, not_1_out, not_2_out, not_3_out, not_4_out, not_5_out,
       not_6_out, not_7_out, not_8_out, not_9_out, not_10_out, not_11_out, s_r_ff_8_q;

  not not_1 (not_1_out, nPE);
  not not_2 (not_2_out, not_1_out);
  buf buffer_1 (buffer_1_out, DS);
  buf buffer_2 (buffer_2_out, CP);
  buf buffer_3 (buffer_3_out, nCE);
  not not_3 (not_3_out, nMR);
  buf buffer_4 (buffer_4_out, D0);
  and and_1 (and_1_out, buffer_1_out, not_2_out);
  and and_2 (and_2_out, not_1_out, buffer_4_out);
  nor nor_1 (nor_1_out, and_1_out, and_2_out);
  not not_4 (not_4_out, nor_1_out);
  nor nor_2 (nor_2_out, buffer_2_out, buffer_3_out);
  and and_3 (and_3_out, test[0], not_2_out);
  nor nor_3 (nor_3_out, and_3_out, and_5_out);
  not not_5 (not_5_out, nor_3_out);
  S_R_Flip_Flop #(.trigger("falling")) s_r_ff_1 (
    .S(not_4_out), .clk(nor_2_out), .R(nor_1_out), .Q(test[0]), .reset(not_3_out), .en(1'b1));  // open: Qn, preset
  buf buffer_5 (buffer_5_out, D1);
  and and_4 (and_4_out, test[1], not_2_out);
  and and_5 (and_5_out, not_1_out, buffer_5_out);
  S_R_Flip_Flop #(.trigger("falling")) s_r_ff_2 (
    .S(not_5_out), .clk(nor_2_out), .R(nor_3_out), .Q(test[1]), .reset(not_3_out), .en(1'b1));  // open: Qn, preset
  buf buffer_6 (buffer_6_out, D2);
  and and_6 (and_6_out, not_1_out, buffer_6_out);
  nor nor_4 (nor_4_out, and_4_out, and_6_out);
  not not_6 (not_6_out, nor_4_out);
  S_R_Flip_Flop #(.trigger("falling")) s_r_ff_3 (
    .S(not_6_out), .clk(nor_2_out), .R(nor_4_out), .Q(test[2]), .reset(not_3_out), .en(1'b1));  // open: Qn, preset
  buf buffer_7 (buffer_7_out, D3);
  and and_7 (and_7_out, not_1_out, buffer_7_out);
  and and_8 (and_8_out, test[2], not_2_out);
  nor nor_5 (nor_5_out, and_8_out, and_7_out);
  not not_7 (not_7_out, nor_5_out);
  and and_9 (and_9_out, test[3], not_2_out);
  nor nor_6 (nor_6_out, and_9_out, and_10_out);
  not not_8 (not_8_out, nor_6_out);
  S_R_Flip_Flop #(.trigger("falling")) s_r_ff_4 (
    .S(not_7_out), .clk(nor_2_out), .R(nor_5_out), .Q(test[3]), .reset(not_3_out), .en(1'b1));  // open: Qn, preset
  buf buffer_8 (buffer_8_out, D4);
  and and_10 (and_10_out, not_1_out, buffer_8_out);
  S_R_Flip_Flop #(.trigger("falling")) s_r_ff_5 (
    .S(not_8_out), .clk(nor_2_out), .R(nor_6_out), .Q(test[4]), .reset(not_3_out), .en(1'b1));  // open: Qn, preset
  buf buffer_9 (buffer_9_out, D5);
  and and_11 (and_11_out, test[4], not_2_out);
  and and_12 (and_12_out, not_1_out, buffer_9_out);
  nor nor_7 (nor_7_out, and_11_out, and_12_out);
  not not_9 (not_9_out, nor_7_out);
  S_R_Flip_Flop #(.trigger("falling")) s_r_ff_6 (
    .S(not_9_out), .clk(nor_2_out), .R(nor_7_out), .Q(test[5]), .reset(not_3_out), .en(1'b1));  // open: Qn, preset
  and and_13 (and_13_out, not_1_out, buffer_10_out);
  and and_14 (and_14_out, test[5], not_2_out);
  nor nor_8 (nor_8_out, and_14_out, and_13_out);
  not not_10 (not_10_out, nor_8_out);
  buf buffer_10 (buffer_10_out, D6);
  and and_15 (and_15_out, test[6], not_2_out);
  S_R_Flip_Flop #(.trigger("falling")) s_r_ff_7 (
    .S(not_10_out), .clk(nor_2_out), .R(nor_8_out), .Q(test[6]), .reset(not_3_out), .en(1'b1));  // open: Qn, preset
  buf buffer_11 (buffer_11_out, D7);
  and and_16 (and_16_out, not_1_out, buffer_11_out);
  nor nor_9 (nor_9_out, and_15_out, and_16_out);
  not not_11 (not_11_out, nor_9_out);
  S_R_Flip_Flop #(.trigger("falling")) s_r_ff_8 (
    .S(not_11_out), .clk(nor_2_out), .R(nor_9_out), .Q(s_r_ff_8_q), .reset(not_3_out), .en(1'b1));  // open: Qn, preset
  buf buffer_12 (Q7, s_r_ff_8_q);

  assign test[7] = Q7;
endmodule
