// Logisim project CS1409_U201414800_刘一龙_cpu.circ as structural Verilog: 16 circuits, main circuit MIPS
module MIPS (
);

  wire and_2_out, and_4_out, and_5_out, and_6_out, and_9_out, and_10_out, and_11_out, and_12_out, clk,
       clock_1_out, cnt1_1_value, comparator_1_eq, comparator_2_eq, comparator_3_eq, comparator_3_lt,
       controlunit_1_alusham, controlunit_1_alusrc, controlunit_1_beq, controlunit_1_bgtz, controlunit_1_bne,
       controlunit_1_extop, controlunit_1_jal, controlunit_1_jmp, controlunit_1_lotoreg,
       controlunit_1_rambyte, controlunit_1_ramtoreg, controlunit_1_ramwe, controlunit_1_regdst,
       controlunit_1_regwe, controlunit_1_syscall, controlunit_1_writetolo, counter_1_q, ex_mem_1_bubble,
       ex_mem_1_memlotoreg, ex_mem_1_memrambyte, ex_mem_1_memramtoreg, ex_mem_1_memramwe, ex_mem_1_memregwe,
       ex_mem_1_memsyscall, ex_mem_1_memwritetolo, FlushD, FlushE, forwardunit_1_memforward, Halt,
       id_ex_1_bubble, id_ex_1_exalusham, id_ex_1_exalusrc, id_ex_1_exextop, id_ex_1_exjal,
       id_ex_1_exlotoreg, id_ex_1_exrambyte, id_ex_1_exramtoreg, id_ex_1_exramwe, id_ex_1_exregdst,
       id_ex_1_exregwe, id_ex_1_exsyscall, id_ex_1_exwritetolo, ID_EX_Bubble, if_id_1_bubble,
       if_id_1_id_taken, IF_ID_Bubble, IType, JmpBranch, JmpImm, JmpNeedReg, JmpReg, JType, LoadUseBubble,
       mem_wb_1_bubble, mem_wb_1_wblotoreg, mem_wb_1_wbramtoreg, mem_wb_1_wbregwe, mem_wb_1_wbwritetolo,
       MisPreditctoin, not_1_out, not_2_out, not_3_out, not_4_out, not_5_out, or_1_out, register_1_q, RType,
       Stall, SuccessPreditction, Syscall;
  wire [1:0] forwardunit_1_exforwarda, forwardunit_1_exforwardb, forwardunit_1_idforwarda,
       forwardunit_1_idforwardb;
  wire [3:0] controlunit_1_aluop, id_ex_1_exaluop, multiplexer_4_out_2, multiplexer_4_out_3,
       multiplexer_4_out_4, multiplexer_4_out_5;
  wire [4:0] decoder_1_rd, decoder_1_rs, decoder_1_rt, decoder_1_sham, ex_mem_1_memrt, ex_mem_1_memrw_num,
       id_ex_1_exrd, id_ex_1_exrs, id_ex_1_exrt, id_ex_1_exsham, mem_wb_1_wbrw_num, multiplexer_5_out,
       multiplexer_8_out, multiplexer_9_out;
  wire [5:0] decoder_1_funct, decoder_1_op;
  wire [7:0] multiplexer_18_out;
  wire [15:0] decoder_1_imm16, id_ex_1_eximm16, multiplexer_4_out;
  wire [25:0] decoder_1_imm26;
  wire [31:0] a0, adder_1_out, AddrBranch, AddrImm, AddrReg, alu_1_result, bit_extender_1_out,
       bit_extender_2_out, bit_extender_3_out, bit_extender_4_out, branchpredictor_1_predictaddr,
       counter_2_value, counter_3_value, counter_4_value, counter_5_value, counter_6_value, counter_7_value,
       counter_8_value, ex_mem_1_memir, ex_mem_1_mempc, ex_mem_1_memr2, ex_mem_1_memresult, id_ex_1_exir,
       id_ex_1_expc, id_ex_1_exr1, id_ex_1_exr2, if_id_1_idir, if_id_1_idpc, LO_q, main_1_reg1,
       main_1_reg2_2, mem_wb_1_wbramdata, mem_wb_1_wbresult, multiplexer_1_out, multiplexer_2_out,
       multiplexer_3_out, multiplexer_7_out, multiplexer_10_out, multiplexer_11_out, multiplexer_12_out,
       multiplexer_13_out, multiplexer_14_out, multiplexer_15_out, multiplexer_16_out, multiplexer_17_out,
       multiplexer_19_out, multiplexer_20_out, multiplexer_21_out, PC_q, ra, ram_1_data, rom_1_data, s0, s1,
       s2, v0;

  Clock clock_1 (.out(clock_1_out));
  Adder #(.width(32)) adder_1 (.a(32'h4), .b(if_id_1_idpc), .out(adder_1_out));  // open: cin, cout
  Cnt1 cnt1_1 (.enable(counter_1_q), .clk(clk), .value(cnt1_1_value));
  Counter_part #(.width(1), .max('h1), .ongoal("stay")) counter_1 (
    .load(1'b0), .count(1'b1), .Q(counter_1_q), .clk(Halt), .clr(1'b0));  // open: D, carry
  // Probe on multiplexer_1_out
  Multiplexer #(.width(32), .enable("false")) multiplexer_1 (
    .in0(adder_1_out), .in1(AddrBranch), .out(multiplexer_1_out), .sel(JmpBranch));
  and and_1 (clk, clock_1_out, not_1_out);
  not not_1 (not_1_out, cnt1_1_value);
  Multiplexer #(.width(32), .enable("false")) multiplexer_2 (
    .in0(branchpredictor_1_predictaddr), .in1(multiplexer_1_out), .out(multiplexer_2_out),
    .sel(MisPreditctoin));
  Hex_Digit_Display hex_digit_display_1 (.value(multiplexer_4_out_5));  // open: dp
  Multiplexer #(.width(32), .enable("false")) multiplexer_3 (
    .in0(multiplexer_2_out), .in1(AddrReg), .out(multiplexer_3_out), .sel(JmpReg));
  Hex_Digit_Display hex_digit_display_2 (.value(multiplexer_4_out_3));  // open: dp
  Hex_Digit_Display hex_digit_display_3 (.value(multiplexer_4_out_4));  // open: dp
  Comparator #(.width(32), .mode("unsigned")) comparator_1 (.a(32'ha), .b(v0), .eq(comparator_1_eq));  // open: gt, lt
  Register #(.width(32)) PC (.D(multiplexer_3_out), .en(Stall), .Q(PC_q), .clk(clk), .clr(1'b0));
  Hex_Digit_Display hex_digit_display_4 (.value(multiplexer_4_out_2));  // open: dp
  Hex_Digit_Display hex_digit_display_5 (.value(multiplexer_4_out[15:12]));  // open: dp
  and and_2 (and_2_out, not_2_out, Syscall);
  and and_3 (Halt, comparator_1_eq, Syscall);
  not not_2 (not_2_out, comparator_1_eq);
  Hex_Digit_Display hex_digit_display_6 (.value(multiplexer_4_out[7:4]));  // open: dp
  Hex_Digit_Display hex_digit_display_7 (.value(multiplexer_4_out[11:8]));  // open: dp
  Register #(.width(1)) register_1 (.D(1'b1), .en(and_2_out), .Q(register_1_q), .clk(clk));  // open: clr
  Hex_Digit_Display hex_digit_display_8 (.value(multiplexer_4_out[3:0]));  // open: dp
  Multiplexer #(.width(32), .enable("false")) multiplexer_4 (
    .in0({32{1'b0}}), .in1(a0),
    .out({multiplexer_4_out_5, multiplexer_4_out_4, multiplexer_4_out_3, multiplexer_4_out_2, multiplexer_4_out}),
    .sel(register_1_q));
  ROM #(.addrWidth(10), .dataWidth(32)) rom_1 (.addr(PC_q[11:2]), .data(rom_1_data));  // open: sel
  Counter counter_2 (.clk(clk), .value(counter_2_value));  // open: enable
  // Probe on counter_2_value
  // Probe on branchpredictor_1_predictaddr
  and and_4 (and_4_out, ~ID_EX_Bubble, IF_ID_Bubble);  // AND_Gate
  Counter counter_3 (.enable(and_4_out), .clk(clk), .value(counter_3_value));
  // Probe on counter_3_value
  BranchPredictor branchpredictor_1 (
    .ir(rom_1_data), .pc(PC_q), .taken(1'b1), .PredictAddr(branchpredictor_1_predictaddr));
  Counter counter_4 (.enable(ID_EX_Bubble), .clk(clk), .value(counter_4_value));
  // Probe on counter_4_value
  // Probe on MisPreditctoin
  Counter counter_5 (.enable(LoadUseBubble), .clk(clk), .value(counter_5_value));
  // Probe on counter_5_value
  // Probe on a0
  // Probe on counter_6_value
  and and_5 (and_5_out, ~ID_EX_Bubble, MisPreditctoin);  // AND_Gate
  Counter counter_6 (.enable(and_5_out), .clk(clk), .value(counter_6_value));
  and and_6 (and_6_out, ~ID_EX_Bubble, SuccessPreditction);  // AND_Gate
  Counter counter_7 (.enable(and_6_out), .clk(clk), .value(counter_7_value));
  // Probe on counter_7_value
  Counter counter_8 (.enable(JType), .clk(clk), .value(counter_8_value));
  // Probe on counter_8_value
  IF_ID if_id_1 (
    .clk(clk), .IFPC(PC_q), .IFIR(rom_1_data), .IDPC(if_id_1_idpc), .IDIR(if_id_1_idir), .en(Stall),
    .bubble(if_id_1_bubble), .clr(FlushD), .IF_taken(1'b1), .ID_taken(if_id_1_id_taken));
  LED led_1 (.in(if_id_1_bubble));
  Decoder decoder_1 (
    .instruction(if_id_1_idir), .op(decoder_1_op), .rs(decoder_1_rs), .rt(decoder_1_rt), .rd(decoder_1_rd),
    .sham(decoder_1_sham), .funct(decoder_1_funct), .imm16(decoder_1_imm16), .imm26(decoder_1_imm26));
  Comparator #(.width(1), .mode("unsigned")) comparator_2 (
    .a(JmpBranch), .b(if_id_1_id_taken), .eq(comparator_2_eq));  // open: gt, lt
  or or_1 (or_1_out, controlunit_1_beq, controlunit_1_bne, controlunit_1_bgtz);
  not not_3 (not_3_out, comparator_2_eq);
  and and_7 (MisPreditctoin, or_1_out, not_3_out);
  and and_8 (SuccessPreditction, or_1_out, comparator_2_eq);
  ControlUnit controlunit_1 (
    .op(decoder_1_op), .funct(decoder_1_funct), .ALUOp(controlunit_1_aluop), .RegWe(controlunit_1_regwe),
    .ALUSrc(controlunit_1_alusrc), .RegDst(controlunit_1_regdst), .ExtOp(controlunit_1_extop),
    .ALUSham(controlunit_1_alusham), .RAMtoReg(controlunit_1_ramtoreg), .RAMWe(controlunit_1_ramwe),
    .Beq(controlunit_1_beq), .Bne(controlunit_1_bne), .Jmp(controlunit_1_jmp), .Jr(JmpReg),
    .Jal(controlunit_1_jal), .Syscall(controlunit_1_syscall), .WriteToLO(controlunit_1_writetolo),
    .LOToReg(controlunit_1_lotoreg), .RAMByte(controlunit_1_rambyte), .Bgtz(controlunit_1_bgtz),
    .RType(RType), .ITypee(IType), .JType(JType));
  or or_2 (JmpNeedReg, controlunit_1_beq, controlunit_1_bne, controlunit_1_bgtz, JmpReg);
  ForwardUnit forwardunit_1 (
    .EXForwardA(forwardunit_1_exforwarda), .EXForwardB(forwardunit_1_exforwardb), .ID_EX_rt(id_ex_1_exrt),
    .EX_MEM_RW_num(ex_mem_1_memrw_num), .MEM_WB_RW_num(mem_wb_1_wbrw_num), .ID_EX_rs(id_ex_1_exrs),
    .EX_MEM_RegWe(ex_mem_1_memregwe), .MEM_WB_RegWe(mem_wb_1_wbregwe), .EX_MEM_rt(ex_mem_1_memrt),
    .EX_MEM_RAMWe(ex_mem_1_memramwe), .MEMForward(forwardunit_1_memforward),
    .IDForwardA(forwardunit_1_idforwarda), .ID_rs(multiplexer_5_out), .IDForwardB(forwardunit_1_idforwardb),
    .ID_rt(decoder_1_rt));
  Multiplexer #(.width(5), .enable("false")) multiplexer_5 (
    .in0(decoder_1_rs), .in1(decoder_1_rt), .out(multiplexer_5_out), .sel(controlunit_1_alusham));
  LoadUseHazardDetector loadusehazarddetector_1 (
    .ID_EX_RAMtoReg(id_ex_1_exramtoreg), .LoadUseHazard(LoadUseBubble), .IDrs(multiplexer_5_out),
    .ID_EX_rt(id_ex_1_exrt), .IDrt(decoder_1_rt));
  \CS1409_U201414800_刘一龙_regfile_main  main_1 (
    .Reg1_num(multiplexer_5_out), .Reg2(decoder_1_rt), .Write_Reg_num(mem_wb_1_wbrw_num),
    .Din(multiplexer_20_out), .Write_Enable(mem_wb_1_wbregwe), .Clock(clk), .Reg1(main_1_reg1),
    .Reg2_2(main_1_reg2_2), .s0_Value(s0), .s1_Value(s1), .s2_Value(s2), .ra_Value(ra), .a0(a0), .v0(v0));
  AddressCalculator addresscalculator_1 (
    .pc(if_id_1_idpc), .imm16(decoder_1_imm16), .imm26(decoder_1_imm26), .AddrBranch(AddrBranch),
    .AddrImm(AddrImm));
  or or_3 (JmpImm, controlunit_1_jmp, controlunit_1_jal);
  Multiplexer #(.select(2), .width(32), .enable("false")) multiplexer_6 (
    .in0(main_1_reg1), .in1(multiplexer_20_out), .in2(ex_mem_1_memresult), .out(AddrReg),
    .sel(forwardunit_1_idforwarda));  // open: in3
  and and_9 (and_9_out, controlunit_1_bne, not_4_out);
  or or_4 (JmpBranch, and_9_out, and_10_out, and_11_out);
  and and_10 (and_10_out, controlunit_1_beq, comparator_3_eq);
  not not_4 (not_4_out, comparator_3_eq);
  Comparator #(.width(32)) comparator_3 (
    .a(AddrReg), .b(multiplexer_7_out), .eq(comparator_3_eq), .lt(comparator_3_lt));  // open: gt
  Multiplexer #(.select(2), .width(32), .enable("false")) multiplexer_7 (
    .in0(main_1_reg2_2), .in1(multiplexer_20_out), .in2(ex_mem_1_memresult), .out(multiplexer_7_out),
    .sel(forwardunit_1_idforwardb));  // open: in3
  and and_11 (and_11_out, controlunit_1_bgtz, not_4_out, not_5_out);
  not not_5 (not_5_out, comparator_3_lt);
  ID_EX id_ex_1 (
    .clk(clk), .IDPC(if_id_1_idpc), .EXPC(id_ex_1_expc), .IDIR(if_id_1_idir), .EXIR(id_ex_1_exir),
    .IDLOtoReg(controlunit_1_lotoreg), .EXLOtoReg(id_ex_1_exlotoreg), .IDSyscall(controlunit_1_syscall),
    .EXSyscall(id_ex_1_exsyscall), .IDRAMWe(controlunit_1_ramwe), .EXRAMWe(id_ex_1_exramwe),
    .IDRAMByte(controlunit_1_rambyte), .EXRAMByte(id_ex_1_exrambyte), .IDALUOp(controlunit_1_aluop),
    .EXALUOp(id_ex_1_exaluop), .IDALUSrc(controlunit_1_alusrc), .EXALUSrc(id_ex_1_exalusrc),
    .IDExtOp(controlunit_1_extop), .EXExtOp(id_ex_1_exextop), .IDALUSham(controlunit_1_alusham),
    .EXALUSham(id_ex_1_exalusham), .IDJal(controlunit_1_jal), .EXJal(id_ex_1_exjal),
    .IDWritetoLO(controlunit_1_writetolo), .EXWritetoLO(id_ex_1_exwritetolo), .IDrt(decoder_1_rt),
    .EXrt(id_ex_1_exrt), .IDrd(decoder_1_rd), .EXrd(id_ex_1_exrd), .IDRegDst(controlunit_1_regdst),
    .EXRegDst(id_ex_1_exregdst), .IDRegWe(controlunit_1_regwe), .EXRegWe(id_ex_1_exregwe),
    .IDRAMtoReg(controlunit_1_ramtoreg), .EXRAMtoReg(id_ex_1_exramtoreg), .IDsham(decoder_1_sham),
    .EXsham(id_ex_1_exsham), .IDimm16(decoder_1_imm16), .EXimm16(id_ex_1_eximm16), .IDR1(AddrReg),
    .EXR1(id_ex_1_exr1), .IDR2(multiplexer_7_out), .EXR2(id_ex_1_exr2), .IDrs(multiplexer_5_out),
    .EXrs(id_ex_1_exrs), .bubble(id_ex_1_bubble), .clr(FlushE));
  LED led_2 (.in(id_ex_1_bubble));
  Multiplexer #(.width(5), .enable("false")) multiplexer_8 (
    .in0(id_ex_1_exrt), .in1(id_ex_1_exrd), .out(multiplexer_8_out), .sel(id_ex_1_exregdst));
  BranchHazardDetector branchhazarddetector_1 (
    .ID_EX_RW_num(multiplexer_9_out), .IDrs(multiplexer_5_out), .FlushE(ID_EX_Bubble), .IDrt(decoder_1_rt),
    .EX_MEM_RW_num(ex_mem_1_memrw_num), .ID_EX_RegWe(id_ex_1_exregwe),
    .EX_MEM_RAMtoReg(ex_mem_1_memramtoreg), .IDJmpReg(JmpReg), .JmpNeedReg(JmpNeedReg),
    .FlushD(IF_ID_Bubble), .IDJmpBranch(MisPreditctoin));
  Multiplexer #(.width(5), .enable("false")) multiplexer_9 (
    .in0(multiplexer_8_out), .in1({5{1'b1}}), .out(multiplexer_9_out), .sel(id_ex_1_exjal));
  Multiplexer #(.select(2), .width(32), .enable("false")) multiplexer_10 (
    .in0(id_ex_1_exr1), .in1(multiplexer_20_out), .in2(ex_mem_1_memresult), .out(multiplexer_10_out),
    .sel(forwardunit_1_exforwarda));  // open: in3
  Multiplexer #(.width(32), .enable("false")) multiplexer_11 (
    .in0(multiplexer_10_out), .in1(id_ex_1_expc), .out(multiplexer_11_out), .sel(id_ex_1_exjal));
  assign bit_extender_1_out = {{16{1'b0}}, id_ex_1_eximm16};  // Bit_Extender bit_extender_1
  assign bit_extender_2_out = {{16{id_ex_1_eximm16[15]}}, id_ex_1_eximm16};  // Bit_Extender bit_extender_2
  Multiplexer #(.select(2), .width(32), .enable("false")) multiplexer_12 (
    .in0(id_ex_1_exr2), .in1(multiplexer_20_out), .in2(ex_mem_1_memresult), .out(multiplexer_12_out),
    .sel(forwardunit_1_exforwardb));  // open: in3
  SynchronousUnit synchronousunit_1 (
    .LoadUseHazard(LoadUseBubble), .BranchFlushE(ID_EX_Bubble), .BranchFlushD(IF_ID_Bubble), .FlushE(FlushE),
    .FlushD(FlushD), .clk(clk), .Stall(Stall));
  Multiplexer #(.width(32), .enable("false")) multiplexer_13 (
    .in0(bit_extender_1_out), .in1(bit_extender_2_out), .out(multiplexer_13_out), .sel(id_ex_1_exextop));
  Multiplexer #(.width(32), .enable("false")) multiplexer_14 (
    .in0(multiplexer_12_out), .in1(multiplexer_13_out), .out(multiplexer_14_out), .sel(id_ex_1_exalusrc));
  assign bit_extender_3_out = {{27{1'b0}}, id_ex_1_exsham};  // Bit_Extender bit_extender_3
  Multiplexer #(.width(32), .enable("false")) multiplexer_15 (
    .in0(multiplexer_14_out), .in1(bit_extender_3_out), .out(multiplexer_15_out), .sel(id_ex_1_exalusham));
  Multiplexer #(.width(32), .enable("false")) multiplexer_16 (
    .in0(multiplexer_15_out), .in1(32'h4), .out(multiplexer_16_out), .sel(id_ex_1_exjal));
  ALU alu_1 (
    .AluOP(id_ex_1_exaluop), .X(multiplexer_11_out), .Result(alu_1_result), .Y(multiplexer_16_out));  // open: Equal, Signed_Overflow, Result_2, UnSigned_Overflow
  EX_MEM ex_mem_1 (
    .clk(clk), .EXPC(id_ex_1_expc), .MEMPC(ex_mem_1_mempc), .EXRegWe(id_ex_1_exregwe),
    .MEMRegWe(ex_mem_1_memregwe), .EXRW_num(multiplexer_9_out), .MEMRW_num(ex_mem_1_memrw_num),
    .EXRAMtoReg(id_ex_1_exramtoreg), .MEMRAMtoReg(ex_mem_1_memramtoreg), .EXIR(id_ex_1_exir),
    .MEMIR(ex_mem_1_memir), .EXLOtoReg(id_ex_1_exlotoreg), .MEMLOtoReg(ex_mem_1_memlotoreg),
    .EXSyscall(id_ex_1_exsyscall), .MEMSyscall(ex_mem_1_memsyscall), .EXRAMWe(id_ex_1_exramwe),
    .MEMRAMWe(ex_mem_1_memramwe), .EXRAMByte(id_ex_1_exrambyte), .MEMRAMByte(ex_mem_1_memrambyte),
    .EXR2(id_ex_1_exr2), .MEMR2(ex_mem_1_memr2), .EXWritetoLO(id_ex_1_exwritetolo),
    .MEMWritetoLO(ex_mem_1_memwritetolo), .EXResult(alu_1_result), .MEMResult(ex_mem_1_memresult),
    .EXrt(id_ex_1_exrt), .MEMrt(ex_mem_1_memrt), .bubble(ex_mem_1_bubble));
  LED led_3 (.in(ex_mem_1_bubble));
  Multiplexer #(.width(32), .enable("false")) multiplexer_17 (
    .in0(ex_mem_1_memr2), .in1(multiplexer_20_out), .out(multiplexer_17_out), .sel(forwardunit_1_memforward));
  and and_12 (and_12_out, ex_mem_1_memramwe, ~Halt);  // AND_Gate
  RAM #(.addrWidth(24), .dataWidth(32), .bus("separate")) ram_1 (
    .addr(ex_mem_1_memresult[25:2]), .din(multiplexer_17_out), .data(ram_1_data), .str(and_12_out),
    .sel(1'b1), .clk(clk), .ld(ex_mem_1_memramtoreg), .clr(1'b0));
  Multiplexer #(.select(2), .width(8), .enable("false")) multiplexer_18 (
    .in0(ram_1_data[7:0]), .in1(ram_1_data[15:8]), .in2(ram_1_data[23:16]), .in3(ram_1_data[31:24]),
    .out(multiplexer_18_out), .sel(ex_mem_1_memresult[1:0]));
  assign bit_extender_4_out = {{24{multiplexer_18_out[7]}}, multiplexer_18_out};  // Bit_Extender bit_extender_4
  Multiplexer #(.width(32), .enable("false")) multiplexer_19 (
    .in0(ram_1_data), .in1(bit_extender_4_out), .out(multiplexer_19_out), .sel(ex_mem_1_memrambyte));
  MEM_WB mem_wb_1 (
    .clk(clk), .MEMPC(ex_mem_1_mempc), .MEMRegWe(ex_mem_1_memregwe), .WBRegWe(mem_wb_1_wbregwe),
    .MEMRW_num(ex_mem_1_memrw_num), .WBRW_num(mem_wb_1_wbrw_num), .MEMRAMtoReg(ex_mem_1_memramtoreg),
    .WBRAMtoReg(mem_wb_1_wbramtoreg), .MEMIR(ex_mem_1_memir), .MEMLOtoReg(ex_mem_1_memlotoreg),
    .WBLOtoReg(mem_wb_1_wblotoreg), .MEMSyscall(ex_mem_1_memsyscall), .WBSyscall(Syscall),
    .MEMWritetoLO(ex_mem_1_memwritetolo), .WBWritetoLO(mem_wb_1_wbwritetolo), .MEMResult(ex_mem_1_memresult),
    .WBResult(mem_wb_1_wbresult), .MEMRAMData(multiplexer_19_out), .WBRAMData(mem_wb_1_wbramdata),
    .bubble(mem_wb_1_bubble));  // open: WBPC, WBIR
  LED led_4 (.in(mem_wb_1_bubble));
  Multiplexer #(.width(32), .enable("false")) multiplexer_20 (
    .in0(multiplexer_21_out), .in1(LO_q), .out(multiplexer_20_out), .sel(mem_wb_1_wblotoreg));
  Register #(.width(32)) LO (.D(mem_wb_1_wbresult), .en(mem_wb_1_wbwritetolo), .Q(LO_q), .clk(clk));  // open: clr
  Multiplexer #(.width(32), .enable("false")) multiplexer_21 (
    .in0(mem_wb_1_wbresult), .in1(mem_wb_1_wbramdata), .out(multiplexer_21_out), .sel(mem_wb_1_wbramtoreg));

  // Notes on the sheet:
  //   Syscall
  //   听说黑底绿字更好看
  //   contents of rom_1 (hex, n*v repeats v):
  //   20110001 8000c05 20110001 20120002 20130003 8000c09 20110001 20120002 20130003 8000c0d 20110001
  //   20120002 20130003 8000c11 20110001 20120002 20130003 c000cb8 20100001 20110001 118fc0 112020
  //   20020022 c 118882 12200001 8000c15 112020 20020022 c 20110001 118880 112020 20020022 c 12200001
  //   8000c1f 20110001 118fc0 112020 20020022 c 1188c3 112020 20020022 c 118903 112020 20020022 c 118903
  //   112020 20020022 c 118903 112020 20020022 c 118903 112020 20020022 c 118903 112020 20020022 c 118903
  //   112020 20020022 c 118903 112020 20020022 c 20100001 109fc0 139fc3 8021 2012000c 24160003 26100001
  //   3210000f 20080008 20090001 139900 2709825 132020 20020022 c 1094022 1500fff9 22100001 2018000f
  //   2188024 108700 20080008 20090001 139902 2709825 132021 20020022 c 1094022 1500fff9 108702 2c9b022
  //   12c00001 8000c50 4020 1084027 84400 3508ffff 82021 20020022 c 2010ffff 20110000 ae300000 22100001
  //   22310004 ae300000 22100001 22310004 ae300000 22100001 22310004 ae300000 22100001 22310004 ae300000
  //   22100001 22310004 ae300000 22100001 22310004 ae300000 22100001 22310004 ae300000 22100001 22310004
  //   ae300000 22100001 22310004 ae300000 22100001 22310004 ae300000 22100001 22310004 ae300000 22100001
  //   22310004 ae300000 22100001 22310004 ae300000 22100001 22310004 ae300000 22100001 22310004 ae300000
  //   22100001 22310004 22100001 8020 2011003c 8e130000 8e340000 274402a 11000002 ae330000 ae140000
  //   2231fffc 1611fff8 102020 20020022 c 22100004 2011003c 1611fff2 2002000a c 20100000 22100001 102020
  //   20020022 c 22100002 102020 20020022 c 22100003 102020 20020022 c 22100004 102020 20020022 c 22100005
  //   102020 20020022 c 22100006 102020 20020022 c 22100007 102020 20020022 c 22100008 102020 20020022
  //   20020022 c 3e00008
  //   Pipeline Count = Single Cycle Count + Jmp + Success Branch + BranchBubble + LoadUseBubble + 4
endmodule

module Decoder (
  input  [31:0] instruction,
  output [25:0] imm26,
  output [15:0] imm16,
  output [5:0] op,
  output [4:0] rs,
  output [4:0] rt,
  output [4:0] rd,
  output [4:0] sham,
  output [5:0] funct
);


  assign funct = instruction[5:0];
  assign imm16 = instruction[15:0];
  assign imm26 = instruction[25:0];
  assign op = instruction[31:26];
  assign rd = instruction[15:11];
  assign rs = instruction[25:21];
  assign rt = instruction[20:16];
  assign sham = instruction[10:6];

  // Notes on the sheet:
  //   R 型指令译码
  //   I 型指令译码
  //   J 型指令译码
endmodule

module InstructionTyper (
  input  [5:0] op,
  input  [5:0] functy,
  output ADD,
  output ADDI,
  output ADDIU,
  output DIVU,
  output ADDU,
  output MFLO,
  output AND,
  output LB,
  output ANDI,
  output BGTZ,
  output SLL,
  output SRA,
  output SRL,
  output SUB,
  output OR,
  output ORI,
  output NOR,
  output LW,
  output SW,
  output BEQ,
  output BNE,
  output SLT,
  output SLTI,
  output SLTU,
  output JMP,
  output JAL,
  output JR,
  output SYSCALL
);

  wire not_1_out, not_2_out, not_3_out, not_4_out, not_5_out, not_6_out, not_7_out, not_8_out, not_9_out,
       not_10_out, not_11_out, not_12_out, not_13_out, not_14_out, not_15_out, not_16_out, not_17_out,
       not_18_out, not_19_out, not_20_out, not_21_out, not_22_out, not_23_out, not_24_out, not_25_out,
       not_26_out, not_27_out, not_28_out, not_29_out, not_30_out, not_31_out, not_32_out, not_33_out,
       not_34_out, not_35_out, not_36_out, not_37_out, not_38_out, not_39_out, not_40_out, not_41_out,
       not_42_out, not_43_out, not_44_out, not_45_out, not_46_out, not_47_out, not_48_out, not_49_out,
       not_50_out, not_51_out, not_52_out, not_53_out, not_54_out, not_55_out, not_56_out, not_57_out,
       not_58_out, not_59_out, not_60_out, not_61_out, not_62_out, not_63_out, not_64_out, not_65_out,
       not_66_out, not_67_out, not_68_out, not_69_out, not_70_out, not_71_out, not_72_out, not_73_out,
       not_74_out, not_75_out, not_76_out, not_77_out, not_78_out, not_79_out, not_80_out, not_81_out,
       not_82_out, not_83_out, not_84_out, not_85_out, not_86_out, not_87_out, not_88_out, not_89_out,
       not_90_out, not_91_out, not_92_out, not_93_out, not_94_out, not_95_out, not_96_out, not_97_out,
       not_98_out, not_99_out, not_100_out, not_101_out, not_102_out, not_103_out, not_104_out, not_105_out,
       not_106_out, not_107_out, not_108_out, not_109_out, not_110_out, not_111_out, not_112_out,
       not_113_out, not_114_out, not_115_out, not_116_out, not_117_out, not_118_out, not_119_out,
       not_120_out, not_121_out, not_122_out, not_123_out, not_124_out, not_125_out, not_126_out,
       not_127_out, not_128_out, not_129_out, not_130_out, not_131_out, not_132_out, not_133_out,
       not_134_out, not_135_out, not_136_out, not_137_out, not_138_out, not_139_out, not_140_out,
       not_141_out, not_142_out, not_143_out, not_144_out, not_145_out, not_146_out, not_147_out,
       not_148_out, not_149_out, not_150_out, not_151_out, not_152_out, not_153_out, not_154_out,
       not_155_out, not_156_out, not_157_out, not_158_out, not_159_out, not_160_out, not_161_out,
       not_162_out, not_163_out, not_164_out, not_165_out, not_166_out, not_167_out, not_168_out,
       not_169_out, not_170_out, not_171_out, not_172_out, not_173_out, not_174_out, not_175_out,
       not_176_out, not_177_out, not_178_out, not_179_out, not_180_out, not_181_out, not_182_out,
       not_183_out, not_184_out, not_185_out, not_186_out, not_187_out, not_188_out, not_189_out,
       not_190_out, not_191_out, not_192_out, not_193_out, not_194_out, not_195_out, not_196_out,
       not_197_out, not_198_out;

  not not_1 (not_1_out, op[5]);
  not not_2 (not_2_out, op[4]);
  not not_3 (not_3_out, op[3]);
  not not_4 (not_4_out, op[2]);
  not not_5 (not_5_out, op[1]);
  not not_6 (not_6_out, op[0]);
  not not_7 (not_7_out, functy[5]);
  not not_8 (not_8_out, functy[2]);
  not not_9 (not_9_out, op[5]);
  not not_10 (not_10_out, op[4]);
  not not_11 (not_11_out, op[3]);
  not not_12 (not_12_out, op[2]);
  not not_13 (not_13_out, op[1]);
  not not_14 (not_14_out, op[0]);
  not not_15 (not_15_out, functy[5]);
  not not_16 (not_16_out, functy[3]);
  not not_17 (not_17_out, functy[2]);
  not not_18 (not_18_out, functy[0]);
  not not_19 (not_19_out, op[4]);
  not not_20 (not_20_out, op[3]);
  not not_21 (not_21_out, op[2]);
  not not_22 (not_22_out, op[1]);
  not not_23 (not_23_out, op[0]);
  not not_24 (not_24_out, op[5]);
  not not_25 (not_25_out, op[4]);
  not not_26 (not_26_out, op[3]);
  and and_1 (LB, op[5], not_19_out, not_20_out, not_21_out, not_22_out, not_23_out);
  and and_2 (BGTZ, not_24_out, not_25_out, not_26_out, op[2], op[1], op[0]);
  and and_3 (DIVU, not_1_out, not_2_out, not_3_out, not_4_out, not_5_out, not_6_out, not_7_out, functy[4], functy[3], not_8_out, functy[1], functy[0]);
  and and_4 (MFLO, not_9_out, not_10_out, not_11_out, not_12_out, not_13_out, not_14_out, not_15_out, functy[4], not_16_out, not_17_out, functy[1], not_18_out);
  not not_27 (not_27_out, op[5]);
  not not_28 (not_28_out, op[4]);
  not not_29 (not_29_out, op[3]);
  not not_30 (not_30_out, op[2]);
  not not_31 (not_31_out, op[1]);
  not not_32 (not_32_out, op[0]);
  not not_33 (not_33_out, functy[4]);
  not not_34 (not_34_out, functy[3]);
  not not_35 (not_35_out, functy[2]);
  not not_36 (not_36_out, functy[1]);
  not not_37 (not_37_out, functy[0]);
  not not_38 (not_38_out, op[5]);
  not not_39 (not_39_out, op[4]);
  not not_40 (not_40_out, op[2]);
  not not_41 (not_41_out, op[1]);
  not not_42 (not_42_out, op[0]);
  not not_43 (not_43_out, op[5]);
  not not_44 (not_44_out, op[4]);
  not not_45 (not_45_out, op[2]);
  not not_46 (not_46_out, op[1]);
  not not_47 (not_47_out, op[5]);
  not not_48 (not_48_out, op[4]);
  not not_49 (not_49_out, op[3]);
  not not_50 (not_50_out, op[2]);
  not not_51 (not_51_out, op[1]);
  not not_52 (not_52_out, op[0]);
  not not_53 (not_53_out, functy[4]);
  not not_54 (not_54_out, functy[3]);
  not not_55 (not_55_out, functy[2]);
  not not_56 (not_56_out, functy[1]);
  not not_57 (not_57_out, op[5]);
  not not_58 (not_58_out, op[4]);
  not not_59 (not_59_out, op[3]);
  not not_60 (not_60_out, op[2]);
  not not_61 (not_61_out, op[1]);
  not not_62 (not_62_out, op[0]);
  not not_63 (not_63_out, functy[4]);
  not not_64 (not_64_out, functy[3]);
  not not_65 (not_65_out, functy[1]);
  not not_66 (not_66_out, functy[0]);
  not not_67 (not_67_out, op[5]);
  not not_68 (not_68_out, op[4]);
  not not_69 (not_69_out, op[1]);
  not not_70 (not_70_out, op[0]);
  not not_71 (not_71_out, op[5]);
  not not_72 (not_72_out, op[4]);
  not not_73 (not_73_out, op[3]);
  not not_74 (not_74_out, op[2]);
  not not_75 (not_75_out, op[1]);
  not not_76 (not_76_out, op[0]);
  not not_77 (not_77_out, functy[5]);
  not not_78 (not_78_out, functy[4]);
  not not_79 (not_79_out, functy[3]);
  not not_80 (not_80_out, functy[2]);
  not not_81 (not_81_out, functy[1]);
  not not_82 (not_82_out, functy[0]);
  not not_83 (not_83_out, op[5]);
  not not_84 (not_84_out, op[4]);
  not not_85 (not_85_out, op[3]);
  not not_86 (not_86_out, op[2]);
  not not_87 (not_87_out, op[1]);
  not not_88 (not_88_out, op[0]);
  not not_89 (not_89_out, functy[5]);
  not not_90 (not_90_out, functy[4]);
  not not_91 (not_91_out, functy[3]);
  not not_92 (not_92_out, functy[2]);
  not not_93 (not_93_out, op[5]);
  not not_94 (not_94_out, op[4]);
  not not_95 (not_95_out, op[3]);
  not not_96 (not_96_out, op[2]);
  not not_97 (not_97_out, op[1]);
  not not_98 (not_98_out, op[0]);
  not not_99 (not_99_out, functy[5]);
  not not_100 (not_100_out, functy[4]);
  not not_101 (not_101_out, functy[3]);
  not not_102 (not_102_out, functy[2]);
  not not_103 (not_103_out, functy[0]);
  not not_104 (not_104_out, op[5]);
  not not_105 (not_105_out, op[4]);
  not not_106 (not_106_out, op[3]);
  not not_107 (not_107_out, op[2]);
  not not_108 (not_108_out, op[1]);
  not not_109 (not_109_out, op[0]);
  not not_110 (not_110_out, functy[4]);
  not not_111 (not_111_out, functy[3]);
  not not_112 (not_112_out, functy[2]);
  not not_113 (not_113_out, functy[0]);
  not not_114 (not_114_out, op[5]);
  not not_115 (not_115_out, op[4]);
  not not_116 (not_116_out, op[3]);
  not not_117 (not_117_out, op[2]);
  not not_118 (not_118_out, op[1]);
  not not_119 (not_119_out, op[0]);
  not not_120 (not_120_out, functy[4]);
  not not_121 (not_121_out, functy[3]);
  not not_122 (not_122_out, functy[1]);
  not not_123 (not_123_out, op[5]);
  not not_124 (not_124_out, op[4]);
  not not_125 (not_125_out, op[1]);
  not not_126 (not_126_out, op[5]);
  not not_127 (not_127_out, op[4]);
  not not_128 (not_128_out, op[3]);
  not not_129 (not_129_out, op[2]);
  not not_130 (not_130_out, op[1]);
  not not_131 (not_131_out, op[0]);
  not not_132 (not_132_out, functy[4]);
  not not_133 (not_133_out, functy[3]);
  not not_134 (not_134_out, op[4]);
  not not_135 (not_135_out, op[3]);
  not not_136 (not_136_out, op[2]);
  not not_137 (not_137_out, op[4]);
  not not_138 (not_138_out, op[2]);
  not not_139 (not_139_out, op[5]);
  not not_140 (not_140_out, op[4]);
  not not_141 (not_141_out, op[3]);
  not not_142 (not_142_out, op[1]);
  not not_143 (not_143_out, op[0]);
  not not_144 (not_144_out, op[5]);
  not not_145 (not_145_out, op[4]);
  not not_146 (not_146_out, op[3]);
  not not_147 (not_147_out, op[1]);
  not not_148 (not_148_out, op[5]);
  not not_149 (not_149_out, op[4]);
  not not_150 (not_150_out, op[3]);
  not not_151 (not_151_out, op[2]);
  not not_152 (not_152_out, op[1]);
  not not_153 (not_153_out, op[0]);
  not not_154 (not_154_out, functy[4]);
  not not_155 (not_155_out, functy[2]);
  not not_156 (not_156_out, functy[0]);
  not not_157 (not_157_out, op[5]);
  not not_158 (not_158_out, op[4]);
  not not_159 (not_159_out, op[2]);
  not not_160 (not_160_out, op[0]);
  not not_161 (not_161_out, op[5]);
  not not_162 (not_162_out, op[4]);
  not not_163 (not_163_out, op[3]);
  not not_164 (not_164_out, op[2]);
  not not_165 (not_165_out, op[1]);
  not not_166 (not_166_out, op[0]);
  not not_167 (not_167_out, functy[4]);
  not not_168 (not_168_out, functy[2]);
  not not_169 (not_169_out, op[5]);
  not not_170 (not_170_out, op[4]);
  not not_171 (not_171_out, op[3]);
  not not_172 (not_172_out, op[2]);
  not not_173 (not_173_out, op[0]);
  not not_174 (not_174_out, op[5]);
  not not_175 (not_175_out, op[4]);
  not not_176 (not_176_out, op[3]);
  not not_177 (not_177_out, op[2]);
  not not_178 (not_178_out, op[5]);
  not not_179 (not_179_out, op[4]);
  not not_180 (not_180_out, op[3]);
  not not_181 (not_181_out, op[2]);
  not not_182 (not_182_out, op[1]);
  not not_183 (not_183_out, op[0]);
  not not_184 (not_184_out, functy[5]);
  not not_185 (not_185_out, functy[4]);
  not not_186 (not_186_out, functy[2]);
  not not_187 (not_187_out, functy[1]);
  not not_188 (not_188_out, functy[0]);
  not not_189 (not_189_out, op[5]);
  not not_190 (not_190_out, op[4]);
  not not_191 (not_191_out, op[3]);
  not not_192 (not_192_out, op[2]);
  not not_193 (not_193_out, op[1]);
  not not_194 (not_194_out, op[0]);
  not not_195 (not_195_out, functy[5]);
  not not_196 (not_196_out, functy[4]);
  not not_197 (not_197_out, functy[1]);
  not not_198 (not_198_out, functy[0]);
  and and_5 (ADD, not_27_out, not_28_out, not_29_out, not_30_out, not_31_out, not_32_out, functy[5], not_33_out, not_34_out, not_35_out, not_36_out, not_37_out);
  and and_6 (ADDI, not_38_out, not_39_out, op[3], not_40_out, not_41_out, not_42_out);
  and and_7 (ADDIU, not_43_out, not_44_out, op[3], not_45_out, not_46_out, op[0]);
  and and_8 (ADDU, not_47_out, not_48_out, not_49_out, not_50_out, not_51_out, not_52_out, functy[5], not_53_out, not_54_out, not_55_out, not_56_out, functy[0]);
  and and_9 (AND, not_57_out, not_58_out, not_59_out, not_60_out, not_61_out, not_62_out, functy[5], not_63_out, not_64_out, functy[2], not_65_out, not_66_out);
  and and_10 (ANDI, not_67_out, not_68_out, op[3], op[2], not_69_out, not_70_out);
  and and_11 (SLL, not_71_out, not_72_out, not_73_out, not_74_out, not_75_out, not_76_out, not_77_out, not_78_out, not_79_out, not_80_out, not_81_out, not_82_out);
  and and_12 (SRA, not_83_out, not_84_out, not_85_out, not_86_out, not_87_out, not_88_out, not_89_out, not_90_out, not_91_out, not_92_out, functy[1], functy[0]);
  and and_13 (SRL, not_93_out, not_94_out, not_95_out, not_96_out, not_97_out, not_98_out, not_99_out, not_100_out, not_101_out, not_102_out, functy[1], not_103_out);
  and and_14 (SUB, not_104_out, not_105_out, not_106_out, not_107_out, not_108_out, not_109_out, functy[5], not_110_out, not_111_out, not_112_out, functy[1], not_113_out);
  and and_15 (OR, not_114_out, not_115_out, not_116_out, not_117_out, not_118_out, not_119_out, functy[5], not_120_out, not_121_out, functy[2], not_122_out, functy[0]);
  and and_16 (ORI, not_123_out, not_124_out, op[3], op[2], not_125_out, op[0]);
  and and_17 (NOR, not_126_out, not_127_out, not_128_out, not_129_out, not_130_out, not_131_out, functy[5], not_132_out, not_133_out, functy[2], functy[1], functy[0]);
  and and_18 (LW, op[5], not_134_out, not_135_out, not_136_out, op[1], op[0]);
  and and_19 (SW, op[5], not_137_out, op[3], not_138_out, op[1], op[0]);
  and and_20 (BEQ, not_139_out, not_140_out, not_141_out, op[2], not_142_out, not_143_out);
  and and_21 (BNE, not_144_out, not_145_out, not_146_out, op[2], not_147_out, op[0]);
  and and_22 (SLT, not_148_out, not_149_out, not_150_out, not_151_out, not_152_out, not_153_out, functy[5], not_154_out, functy[3], not_155_out, functy[1], not_156_out);
  and and_23 (SLTI, not_157_out, not_158_out, op[3], not_159_out, op[1], not_160_out);
  and and_24 (SLTU, not_161_out, not_162_out, not_163_out, not_164_out, not_165_out, not_166_out, functy[5], not_167_out, functy[3], not_168_out, functy[1], functy[0]);
  and and_25 (JMP, not_169_out, not_170_out, not_171_out, not_172_out, op[1], not_173_out);
  and and_26 (JAL, not_174_out, not_175_out, not_176_out, not_177_out, op[1], op[0]);
  and and_27 (JR, not_178_out, not_179_out, not_180_out, not_181_out, not_182_out, not_183_out, not_184_out, not_185_out, functy[3], not_186_out, not_187_out, not_188_out);
  and and_28 (SYSCALL, not_189_out, not_190_out, not_191_out, not_192_out, not_193_out, not_194_out, not_195_out, not_196_out, functy[3], functy[2], not_197_out, not_198_out);

  // Other names for the same wires on the sheet: FU0 = functy[0]; FU1 = functy[1]; FU2 = functy[2]; FU3 = functy[3];
  //   FU4 = functy[4]; FU5 = functy[5]
endmodule

module ControlUnit (
  input  [5:0] op,
  input  [5:0] funct,
  output [3:0] ALUOp,
  output ALUSrc,
  output RegDst,
  output ExtOp,
  output ALUSham,
  output RAMtoReg,
  output RAMWe,
  output Beq,
  output Bne,
  output Jmp,
  output Jal,
  output Jr,
  output Syscall,
  output WriteToLO,
  output LOToReg,
  output RAMByte,
  output Bgtz,
  output RegWe,
  output RType,
  output ITypee,
  output JType
);

  wire instructiontyper_1_add, instructiontyper_1_addi, instructiontyper_1_addiu, instructiontyper_1_addu,
       instructiontyper_1_and, instructiontyper_1_andi, instructiontyper_1_lw, instructiontyper_1_nor,
       instructiontyper_1_or, instructiontyper_1_ori, instructiontyper_1_sll, instructiontyper_1_slt,
       instructiontyper_1_slti, instructiontyper_1_sltu, instructiontyper_1_sra, instructiontyper_1_srl,
       instructiontyper_1_sub, instructiontyper_2_add, instructiontyper_2_addi, instructiontyper_2_addiu,
       instructiontyper_2_addu, instructiontyper_2_and, instructiontyper_2_andi, instructiontyper_2_beq,
       instructiontyper_2_bgtz, instructiontyper_2_bne, instructiontyper_2_divu, instructiontyper_2_jal,
       instructiontyper_2_jmp, instructiontyper_2_jr, instructiontyper_2_lb, instructiontyper_2_lw,
       instructiontyper_2_mflo, instructiontyper_2_nor, instructiontyper_2_or, instructiontyper_2_ori,
       instructiontyper_2_sll, instructiontyper_2_slt, instructiontyper_2_slti, instructiontyper_2_sltu,
       instructiontyper_2_sra, instructiontyper_2_srl, instructiontyper_2_sub, instructiontyper_2_sw,
       instructiontyper_2_syscall;

  InstructionTyper instructiontyper_1 (
    .op(op), .functy(funct), .ADD(instructiontyper_1_add), .ADDI(instructiontyper_1_addi),
    .ADDIU(instructiontyper_1_addiu), .ADDU(instructiontyper_1_addu), .AND(instructiontyper_1_and),
    .ANDI(instructiontyper_1_andi), .SLL(instructiontyper_1_sll), .SRA(instructiontyper_1_sra),
    .SRL(instructiontyper_1_srl), .SUB(instructiontyper_1_sub), .OR(instructiontyper_1_or),
    .ORI(instructiontyper_1_ori), .NOR(instructiontyper_1_nor), .LW(instructiontyper_1_lw), .SW(RAMWe),
    .BEQ(Beq), .BNE(Bne), .SLT(instructiontyper_1_slt), .SLTI(instructiontyper_1_slti),
    .SLTU(instructiontyper_1_sltu), .JMP(Jmp), .JAL(Jal), .JR(Jr), .SYSCALL(Syscall), .DIVU(WriteToLO),
    .MFLO(LOToReg), .LB(RAMByte), .BGTZ(Bgtz));
  InstructionTyper instructiontyper_2 (
    .op(op), .functy(funct), .ADD(instructiontyper_2_add), .ADDI(instructiontyper_2_addi),
    .ADDIU(instructiontyper_2_addiu), .ADDU(instructiontyper_2_addu), .AND(instructiontyper_2_and),
    .ANDI(instructiontyper_2_andi), .SLL(instructiontyper_2_sll), .SRA(instructiontyper_2_sra),
    .SRL(instructiontyper_2_srl), .SUB(instructiontyper_2_sub), .OR(instructiontyper_2_or),
    .ORI(instructiontyper_2_ori), .NOR(instructiontyper_2_nor), .LW(instructiontyper_2_lw),
    .SW(instructiontyper_2_sw), .BEQ(instructiontyper_2_beq), .BNE(instructiontyper_2_bne),
    .SLT(instructiontyper_2_slt), .SLTI(instructiontyper_2_slti), .SLTU(instructiontyper_2_sltu),
    .JMP(instructiontyper_2_jmp), .JAL(instructiontyper_2_jal), .JR(instructiontyper_2_jr),
    .SYSCALL(instructiontyper_2_syscall), .DIVU(instructiontyper_2_divu), .MFLO(instructiontyper_2_mflo),
    .LB(instructiontyper_2_lb), .BGTZ(instructiontyper_2_bgtz));
  or or_1 (ALUOp[0], instructiontyper_1_add, instructiontyper_1_addi, instructiontyper_1_addiu, instructiontyper_1_addu, instructiontyper_1_and, instructiontyper_1_andi, instructiontyper_1_sra, instructiontyper_1_lw, RAMWe, instructiontyper_1_slt, instructiontyper_1_slti, Jal, RAMByte, Bgtz);
  or or_2 (ALUOp[1], instructiontyper_1_and, instructiontyper_1_andi, instructiontyper_1_srl, instructiontyper_1_sub, instructiontyper_1_nor, instructiontyper_1_slt, instructiontyper_1_slti, Bgtz);
  or or_3 (RType, instructiontyper_2_add, instructiontyper_2_addu, instructiontyper_2_and, instructiontyper_2_sll, instructiontyper_2_sra, instructiontyper_2_srl, instructiontyper_2_sub, instructiontyper_2_or, instructiontyper_2_nor, instructiontyper_2_slt, instructiontyper_2_sltu, instructiontyper_2_jr, instructiontyper_2_syscall, instructiontyper_2_divu, instructiontyper_2_mflo);
  or or_4 (ALUOp[2], instructiontyper_1_add, instructiontyper_1_addi, instructiontyper_1_addiu, instructiontyper_1_addu, instructiontyper_1_and, instructiontyper_1_andi, instructiontyper_1_sub, instructiontyper_1_lw, RAMWe, instructiontyper_1_sltu, Jal, WriteToLO, RAMByte);
  or or_5 (ITypee, instructiontyper_2_addi, instructiontyper_2_addiu, instructiontyper_2_andi, instructiontyper_2_ori, instructiontyper_2_lw, instructiontyper_2_sw, instructiontyper_2_beq, instructiontyper_2_bne, instructiontyper_2_slti, instructiontyper_2_lb, instructiontyper_2_bgtz);
  or or_6 (ALUOp[3], instructiontyper_1_or, instructiontyper_1_ori, instructiontyper_1_nor, instructiontyper_1_slt, instructiontyper_1_slti, instructiontyper_1_sltu, Bgtz);
  or or_7 (JType, instructiontyper_2_jmp, instructiontyper_2_jal);
  or or_8 (RegWe, instructiontyper_1_add, instructiontyper_1_addi, instructiontyper_1_addiu, instructiontyper_1_addu, instructiontyper_1_and, instructiontyper_1_andi, instructiontyper_1_sll, instructiontyper_1_sra, instructiontyper_1_srl, instructiontyper_1_sub, instructiontyper_1_or, instructiontyper_1_ori, instructiontyper_1_nor, instructiontyper_1_lw, instructiontyper_1_slt, instructiontyper_1_slti, instructiontyper_1_sltu, Jal, LOToReg, RAMByte);
  or or_9 (ALUSrc, instructiontyper_1_addi, instructiontyper_1_addiu, instructiontyper_1_andi, instructiontyper_1_ori, instructiontyper_1_lw, RAMWe, instructiontyper_1_slti, RAMByte);
  or or_10 (RegDst, instructiontyper_1_add, instructiontyper_1_addu, instructiontyper_1_and, instructiontyper_1_sll, instructiontyper_1_sra, instructiontyper_1_srl, instructiontyper_1_sub, instructiontyper_1_or, instructiontyper_1_nor, instructiontyper_1_slt, instructiontyper_1_sltu, LOToReg);
  or or_11 (ExtOp, instructiontyper_1_addi, instructiontyper_1_addiu, instructiontyper_1_lw, RAMWe, instructiontyper_1_slti, RAMByte);
  or or_12 (ALUSham, instructiontyper_1_sll, instructiontyper_1_sra, instructiontyper_1_srl);
  or or_13 (RAMtoReg, instructiontyper_1_lw, RAMByte);
endmodule

module ForwardUnit (
  input  MEM_WB_RegWe,
  input  [4:0] MEM_WB_RW_num,
  input  EX_MEM_RegWe,
  input  [4:0] ID_EX_rs,
  input  [4:0] EX_MEM_RW_num,
  input  [4:0] ID_EX_rt,
  input  EX_MEM_RAMWe,
  input  [4:0] EX_MEM_rt,
  input  [4:0] ID_rs,
  input  [4:0] ID_rt,
  output [1:0] EXForwardA,
  output [1:0] EXForwardB,
  output MEMForward,
  output [1:0] IDForwardA,
  output [1:0] IDForwardB
);

  wire and_1_out, and_2_out, and_3_out, and_4_out, and_6_out, and_7_out, and_8_out, and_9_out,
       comparator_1_eq, comparator_2_eq, comparator_3_eq, comparator_4_eq, comparator_5_eq, comparator_6_eq,
       comparator_7_eq, comparator_8_eq, comparator_9_eq, comparator_10_eq, comparator_11_eq,
       comparator_12_eq, comparator_13_eq, comparator_14_eq, comparator_15_eq, comparator_16_eq,
       comparator_17_eq;
  wire [1:0] multiplexer_1_out, multiplexer_2_out, multiplexer_3_out, multiplexer_4_out;

  Comparator #(.width(5), .mode("unsigned")) comparator_1 (
    .a(ID_EX_rs), .b({5{1'b0}}), .eq(comparator_1_eq));  // open: gt, lt
  Comparator #(.width(5), .mode("unsigned")) comparator_2 (
    .a(ID_EX_rs), .b(MEM_WB_RW_num), .eq(comparator_2_eq));  // open: gt, lt
  Comparator #(.width(5), .mode("unsigned")) comparator_3 (
    .a(ID_EX_rs), .b({5{1'b0}}), .eq(comparator_3_eq));  // open: gt, lt
  Comparator #(.width(5), .mode("unsigned")) comparator_4 (
    .a(ID_EX_rs), .b(EX_MEM_RW_num), .eq(comparator_4_eq));  // open: gt, lt
  Comparator #(.width(5), .mode("unsigned")) comparator_5 (
    .a(ID_EX_rt), .b({5{1'b0}}), .eq(comparator_5_eq));  // open: gt, lt
  Comparator #(.width(5), .mode("unsigned")) comparator_6 (
    .a(ID_EX_rt), .b(MEM_WB_RW_num), .eq(comparator_6_eq));  // open: gt, lt
  Comparator #(.width(5), .mode("unsigned")) comparator_7 (
    .a(ID_EX_rt), .b({5{1'b0}}), .eq(comparator_7_eq));  // open: gt, lt
  Comparator #(.width(5), .mode("unsigned")) comparator_8 (
    .a(ID_EX_rt), .b(EX_MEM_RW_num), .eq(comparator_8_eq));  // open: gt, lt
  Comparator #(.width(5), .mode("unsigned")) comparator_9 (
    .a(EX_MEM_rt), .b(MEM_WB_RW_num), .eq(comparator_9_eq));  // open: gt, lt
  Comparator #(.width(5), .mode("unsigned")) comparator_10 (
    .a(ID_rs), .b({5{1'b0}}), .eq(comparator_10_eq));  // open: gt, lt
  Comparator #(.width(5), .mode("unsigned")) comparator_11 (
    .a(ID_rs), .b(MEM_WB_RW_num), .eq(comparator_11_eq));  // open: gt, lt
  Comparator #(.width(5), .mode("unsigned")) comparator_12 (
    .a(ID_rs), .b({5{1'b0}}), .eq(comparator_12_eq));  // open: gt, lt
  Comparator #(.width(5), .mode("unsigned")) comparator_13 (
    .a(ID_rs), .b(EX_MEM_RW_num), .eq(comparator_13_eq));  // open: gt, lt
  Comparator #(.width(5), .mode("unsigned")) comparator_14 (
    .a(ID_rt), .b({5{1'b0}}), .eq(comparator_14_eq));  // open: gt, lt
  Comparator #(.width(5), .mode("unsigned")) comparator_15 (
    .a(ID_rt), .b(MEM_WB_RW_num), .eq(comparator_15_eq));  // open: gt, lt
  Comparator #(.width(5), .mode("unsigned")) comparator_16 (
    .a(ID_rt), .b({5{1'b0}}), .eq(comparator_16_eq));  // open: gt, lt
  Comparator #(.width(5), .mode("unsigned")) comparator_17 (
    .a(ID_rt), .b(EX_MEM_RW_num), .eq(comparator_17_eq));  // open: gt, lt
  and and_1 (and_1_out, MEM_WB_RegWe, ~comparator_1_eq, comparator_2_eq);  // AND_Gate
  and and_2 (and_2_out, EX_MEM_RegWe, ~comparator_3_eq, comparator_4_eq);  // AND_Gate
  and and_3 (and_3_out, MEM_WB_RegWe, ~comparator_5_eq, comparator_6_eq);  // AND_Gate
  and and_4 (and_4_out, EX_MEM_RegWe, ~comparator_7_eq, comparator_8_eq);  // AND_Gate
  and and_5 (MEMForward, MEM_WB_RegWe, EX_MEM_RAMWe, comparator_9_eq);
  and and_6 (and_6_out, MEM_WB_RegWe, ~comparator_10_eq, comparator_11_eq);  // AND_Gate
  and and_7 (and_7_out, EX_MEM_RegWe, ~comparator_12_eq, comparator_13_eq);  // AND_Gate
  and and_8 (and_8_out, MEM_WB_RegWe, ~comparator_14_eq, comparator_15_eq);  // AND_Gate
  and and_9 (and_9_out, EX_MEM_RegWe, ~comparator_16_eq, comparator_17_eq);  // AND_Gate
  Multiplexer #(.width(2), .enable("false")) multiplexer_1 (
    .in0(2'b00), .in1(2'b01), .out(multiplexer_1_out), .sel(and_1_out));
  Multiplexer #(.width(2), .enable("false")) multiplexer_2 (
    .in0(2'b00), .in1(2'b01), .out(multiplexer_2_out), .sel(and_3_out));
  Multiplexer #(.width(2), .enable("false")) multiplexer_3 (
    .in0(2'b00), .in1(2'b01), .out(multiplexer_3_out), .sel(and_6_out));
  Multiplexer #(.width(2), .enable("false")) multiplexer_4 (
    .in0(2'b00), .in1(2'b01), .out(multiplexer_4_out), .sel(and_8_out));
  Multiplexer #(.width(2), .enable("false")) multiplexer_5 (
    .in0(multiplexer_1_out), .in1(2'b10), .out(EXForwardA), .sel(and_2_out));
  Multiplexer #(.width(2), .enable("false")) multiplexer_6 (
    .in0(multiplexer_2_out), .in1(2'b10), .out(EXForwardB), .sel(and_4_out));
  Multiplexer #(.width(2), .enable("false")) multiplexer_7 (
    .in0(multiplexer_3_out), .in1(2'b10), .out(IDForwardA), .sel(and_7_out));
  Multiplexer #(.width(2), .enable("false")) multiplexer_8 (
    .in0(multiplexer_4_out), .in1(2'b10), .out(IDForwardB), .sel(and_9_out));
endmodule

module LoadUseHazardDetector (
  input  ID_EX_RAMtoReg,
  input  [4:0] ID_EX_rt,
  input  [4:0] IDrs,
  input  [4:0] IDrt,
  output LoadUseHazard
);

  wire comparator_1_eq, comparator_2_eq, comparator_3_eq, or_1_out;

  Comparator #(.width(5), .mode("unsigned")) comparator_1 (
    .a(ID_EX_rt), .b(IDrs), .eq(comparator_1_eq));  // open: gt, lt
  Comparator #(.width(5), .mode("unsigned")) comparator_2 (
    .a(ID_EX_rt), .b(IDrt), .eq(comparator_2_eq));  // open: gt, lt
  Comparator #(.width(5), .mode("unsigned")) comparator_3 (
    .a(ID_EX_rt), .b({5{1'b0}}), .eq(comparator_3_eq));  // open: gt, lt
  or or_1 (or_1_out, comparator_1_eq, comparator_2_eq);
  and and_1 (LoadUseHazard, ID_EX_RAMtoReg, or_1_out, ~comparator_3_eq);  // AND_Gate
endmodule

module BranchHazardDetector (
  input  JmpNeedReg,
  input  [4:0] ID_EX_RW_num,
  input  [4:0] IDrs,
  input  [4:0] IDrt,
  input  ID_EX_RegWe,
  input  [4:0] EX_MEM_RW_num,
  input  EX_MEM_RAMtoReg,
  input  IDJmpReg,
  input  IDJmpBranch,
  output FlushE,
  output FlushD
);

  wire and_1_out, and_2_out, comparator_1_eq, comparator_2_eq, comparator_3_eq, comparator_4_eq,
       comparator_5_eq, comparator_6_eq, or_2_out, or_3_out;

  Comparator #(.width(5), .mode("unsigned")) comparator_1 (
    .a(ID_EX_RW_num), .b(IDrs), .eq(comparator_1_eq));  // open: gt, lt
  Comparator #(.width(5), .mode("unsigned")) comparator_2 (
    .a(ID_EX_RW_num), .b(IDrt), .eq(comparator_2_eq));  // open: gt, lt
  Comparator #(.width(5), .mode("unsigned")) comparator_3 (
    .a(ID_EX_RW_num), .b({5{1'b0}}), .eq(comparator_3_eq));  // open: gt, lt
  Comparator #(.width(5), .mode("unsigned")) comparator_4 (
    .a(EX_MEM_RW_num), .b(IDrs), .eq(comparator_4_eq));  // open: gt, lt
  Comparator #(.width(5), .mode("unsigned")) comparator_5 (
    .a(EX_MEM_RW_num), .b(IDrt), .eq(comparator_5_eq));  // open: gt, lt
  Comparator #(.width(5), .mode("unsigned")) comparator_6 (
    .a(EX_MEM_RW_num), .b({5{1'b0}}), .eq(comparator_6_eq));  // open: gt, lt
  or or_1 (FlushD, IDJmpReg, IDJmpBranch);
  or or_2 (or_2_out, comparator_1_eq, comparator_2_eq);
  or or_3 (or_3_out, comparator_4_eq, comparator_5_eq);
  and and_1 (and_1_out, JmpNeedReg, or_2_out, ~comparator_3_eq, ID_EX_RegWe);  // AND_Gate
  and and_2 (and_2_out, JmpNeedReg, or_3_out, ~comparator_6_eq, EX_MEM_RAMtoReg);  // AND_Gate
  or or_4 (FlushE, and_1_out, and_2_out);
endmodule

module SynchronousUnit (
  input  clk,
  input  LoadUseHazard,
  input  BranchFlushE,
  input  BranchFlushD,
  output FlushE,
  output FlushD,
  output Stall
);

  wire d_ff_1_q, d_ff_2_q, or_1_out;

  or or_1 (or_1_out, LoadUseHazard, BranchFlushE);
  not not_1 (Stall, or_1_out);
  and and_1 (FlushE, clk, d_ff_1_q);
  D_Flip_Flop #(.trigger("falling")) d_ff_1 (.clk(clk), .D(or_1_out), .Q(d_ff_1_q));  // open: Qn, preset, en, reset
  and and_2 (FlushD, clk, d_ff_2_q);
  D_Flip_Flop d_ff_2 (.clk(clk), .D(BranchFlushD), .Q(d_ff_2_q), .reset(FlushD));  // open: Qn, preset, en
endmodule

module IF_ID (
  input  clk,
  input  en,
  input  clr,
  input  [31:0] IFPC,
  input  [31:0] IFIR,
  input  IF_taken,
  output [31:0] IDPC,
  output bubble,
  output [31:0] IDIR,
  output ID_taken
);

  wire and_1_out;

  and and_1 (and_1_out, en, clr);
  Register #(.width(32)) register_1 (.D(IFPC), .en(en), .Q(IDPC), .clk(clk), .clr(and_1_out));
  Register #(.width(32)) register_2 (.D(IFIR), .en(en), .Q(IDIR), .clk(clk), .clr(and_1_out));
  Register #(.width(1)) register_3 (.D(IF_taken), .en(en), .Q(ID_taken), .clk(clk), .clr(and_1_out));
  Comparator #(.width(32), .mode("unsigned")) comparator_1 (.a(IDIR), .b({32{1'b0}}), .eq(bubble));  // open: gt, lt
endmodule

module ID_EX (
  input  clk,
  input  clr,
  input  [31:0] IDPC,
  input  IDRegWe,
  input  [4:0] IDrt,
  input  IDRAMtoReg,
  input  [4:0] IDrd,
  input  [31:0] IDIR,
  input  IDLOtoReg,
  input  [4:0] IDsham,
  input  IDSyscall,
  input  [15:0] IDimm16,
  input  [31:0] IDR1,
  input  IDRAMWe,
  input  [31:0] IDR2,
  input  IDRAMByte,
  input  [4:0] IDrs,
  input  IDRegDst,
  input  [3:0] IDALUOp,
  input  IDALUSrc,
  input  IDExtOp,
  input  IDALUSham,
  input  IDJal,
  input  IDWritetoLO,
  output [31:0] EXPC,
  output EXRegWe,
  output [4:0] EXrt,
  output EXRAMtoReg,
  output [4:0] EXrd,
  output [31:0] EXIR,
  output EXLOtoReg,
  output [4:0] EXsham,
  output bubble,
  output EXSyscall,
  output [15:0] EXimm16,
  output [31:0] EXR1,
  output EXRAMWe,
  output [31:0] EXR2,
  output EXRAMByte,
  output [4:0] EXrs,
  output EXRegDst,
  output [3:0] EXALUOp,
  output EXALUSrc,
  output EXExtOp,
  output EXALUSham,
  output EXJal,
  output EXWritetoLO
);

  Register #(.width(32)) register_1 (.D(IDPC), .Q(EXPC), .clk(clk), .clr(clr));  // open: en
  Register #(.width(32)) register_2 (.D(IDIR), .Q(EXIR), .clk(clk), .clr(clr));  // open: en
  Comparator #(.width(32), .mode("unsigned")) comparator_1 (.a(EXIR), .b({32{1'b0}}), .eq(bubble));  // open: gt, lt
  Register #(.width(1)) register_3 (.D(IDRegWe), .Q(EXRegWe), .clk(clk), .clr(clr));  // open: en
  Register #(.width(1)) register_4 (.D(IDRAMtoReg), .Q(EXRAMtoReg), .clk(clk), .clr(clr));  // open: en
  Register #(.width(1)) register_5 (.D(IDLOtoReg), .Q(EXLOtoReg), .clk(clk), .clr(clr));  // open: en
  Register #(.width(1)) register_6 (.D(IDSyscall), .Q(EXSyscall), .clk(clk), .clr(clr));  // open: en
  Register #(.width(1)) register_7 (.D(IDRAMWe), .Q(EXRAMWe), .clk(clk), .clr(clr));  // open: en
  Register #(.width(1)) register_8 (.D(IDRAMByte), .Q(EXRAMByte), .clk(clk), .clr(clr));  // open: en
  Register #(.width(1)) register_9 (.D(IDRegDst), .Q(EXRegDst), .clk(clk), .clr(clr));  // open: en
  Register #(.width(4)) register_10 (.D(IDALUOp), .Q(EXALUOp), .clk(clk), .clr(clr));  // open: en
  Register #(.width(1)) register_11 (.D(IDALUSrc), .Q(EXALUSrc), .clk(clk), .clr(clr));  // open: en
  Register #(.width(1)) register_12 (.D(IDExtOp), .Q(EXExtOp), .clk(clk), .clr(clr));  // open: en
  Register #(.width(1)) register_13 (.D(IDALUSham), .Q(EXALUSham), .clk(clk), .clr(clr));  // open: en
  Register #(.width(1)) register_14 (.D(IDJal), .Q(EXJal), .clk(clk), .clr(clr));  // open: en
  Register #(.width(1)) register_15 (.D(IDWritetoLO), .Q(EXWritetoLO), .clk(clk), .clr(clr));  // open: en
  Register #(.width(5)) register_16 (.D(IDrt), .Q(EXrt), .clk(clk), .clr(clr));  // open: en
  Register #(.width(5)) register_17 (.D(IDrd), .Q(EXrd), .clk(clk), .clr(clr));  // open: en
  Register #(.width(5)) register_18 (.D(IDsham), .Q(EXsham), .clk(clk), .clr(clr));  // open: en
  Register #(.width(16)) register_19 (.D(IDimm16), .Q(EXimm16), .clk(clk), .clr(clr));  // open: en
  Register #(.width(32)) register_20 (.D(IDR1), .Q(EXR1), .clk(clk), .clr(clr));  // open: en
  Register #(.width(32)) register_21 (.D(IDR2), .Q(EXR2), .clk(clk), .clr(clr));  // open: en
  Register #(.width(5)) register_22 (.D(IDrs), .Q(EXrs), .clk(clk), .clr(clr));  // open: en
endmodule

module EX_MEM (
  input  clk,
  input  [31:0] EXPC,
  input  EXRegWe,
  input  [4:0] EXRW_num,
  input  EXRAMtoReg,
  input  [31:0] EXR2,
  input  [31:0] EXIR,
  input  EXLOtoReg,
  input  [31:0] EXResult,
  input  EXSyscall,
  input  [4:0] EXrt,
  input  EXWritetoLO,
  input  EXRAMWe,
  input  EXRAMByte,
  output [31:0] MEMPC,
  output MEMRegWe,
  output [4:0] MEMRW_num,
  output MEMRAMtoReg,
  output [31:0] MEMR2,
  output [31:0] MEMIR,
  output MEMLOtoReg,
  output [31:0] MEMResult,
  output bubble,
  output MEMSyscall,
  output [4:0] MEMrt,
  output MEMWritetoLO,
  output MEMRAMWe,
  output MEMRAMByte
);

  Register #(.width(32)) register_1 (.D(EXPC), .Q(MEMPC), .clk(clk));  // open: en, clr
  Register #(.width(32)) register_2 (.D(EXIR), .Q(MEMIR), .clk(clk));  // open: en, clr
  Comparator #(.width(32), .mode("unsigned")) comparator_1 (.a(MEMIR), .b({32{1'b0}}), .eq(bubble));  // open: gt, lt
  Register #(.width(1)) register_3 (.D(EXRegWe), .Q(MEMRegWe), .clk(clk));  // open: en, clr
  Register #(.width(1)) register_4 (.D(EXRAMtoReg), .Q(MEMRAMtoReg), .clk(clk));  // open: en, clr
  Register #(.width(1)) register_5 (.D(EXLOtoReg), .Q(MEMLOtoReg), .clk(clk));  // open: en, clr
  Register #(.width(1)) register_6 (.D(EXSyscall), .Q(MEMSyscall), .clk(clk));  // open: en, clr
  Register #(.width(1)) register_7 (.D(EXWritetoLO), .Q(MEMWritetoLO), .clk(clk));  // open: en, clr
  Register #(.width(1)) register_8 (.D(EXRAMWe), .Q(MEMRAMWe), .clk(clk));  // open: en, clr
  Register #(.width(1)) register_9 (.D(EXRAMByte), .Q(MEMRAMByte), .clk(clk));  // open: en, clr
  Register #(.width(5)) register_10 (.D(EXRW_num), .Q(MEMRW_num), .clk(clk));  // open: en, clr
  Register #(.width(32)) register_11 (.D(EXR2), .Q(MEMR2), .clk(clk));  // open: en, clr
  Register #(.width(32)) register_12 (.D(EXResult), .Q(MEMResult), .clk(clk));  // open: en, clr
  Register #(.width(5)) register_13 (.D(EXrt), .Q(MEMrt), .clk(clk));  // open: en, clr
endmodule

module MEM_WB (
  input  clk,
  input  [31:0] MEMPC,
  input  MEMRegWe,
  input  [4:0] MEMRW_num,
  input  [31:0] MEMResult,
  input  MEMRAMtoReg,
  input  [31:0] MEMIR,
  input  [31:0] MEMRAMData,
  input  MEMLOtoReg,
  input  MEMSyscall,
  input  MEMWritetoLO,
  output [31:0] WBPC,
  output WBRegWe,
  output [4:0] WBRW_num,
  output [31:0] WBResult,
  output WBRAMtoReg,
  output [31:0] WBIR,
  output [31:0] WBRAMData,
  output WBLOtoReg,
  output bubble,
  output WBSyscall,
  output WBWritetoLO
);

  Register #(.width(32)) register_1 (.D(MEMPC), .Q(WBPC), .clk(clk));  // open: en, clr
  Register #(.width(32)) register_2 (.D(MEMIR), .Q(WBIR), .clk(clk));  // open: en, clr
  Comparator #(.width(32), .mode("unsigned")) comparator_1 (.a(WBIR), .b({32{1'b0}}), .eq(bubble));  // open: gt, lt
  Register #(.width(1)) register_3 (.D(MEMRegWe), .Q(WBRegWe), .clk(clk));  // open: en, clr
  Register #(.width(1)) register_4 (.D(MEMRAMtoReg), .Q(WBRAMtoReg), .clk(clk));  // open: en, clr
  Register #(.width(1)) register_5 (.D(MEMLOtoReg), .Q(WBLOtoReg), .clk(clk));  // open: en, clr
  Register #(.width(1)) register_6 (.D(MEMSyscall), .Q(WBSyscall), .clk(clk));  // open: en, clr
  Register #(.width(1)) register_7 (.D(MEMWritetoLO), .Q(WBWritetoLO), .clk(clk));  // open: en, clr
  Register #(.width(5)) register_8 (.D(MEMRW_num), .Q(WBRW_num), .clk(clk));  // open: en, clr
  Register #(.width(32)) register_9 (.D(MEMResult), .Q(WBResult), .clk(clk));  // open: en, clr
  Register #(.width(32)) register_10 (.D(MEMRAMData), .Q(WBRAMData), .clk(clk));  // open: en, clr
endmodule

module Counter (
  input  enable,
  input  clk,
  output [31:0] value
);

  wire [31:0] adder_1_out;

  Register #(.width(32)) register_1 (.D(adder_1_out), .en(enable), .Q(value), .clk(clk));  // open: clr
  Adder #(.width(32)) adder_1 (.a(32'h1), .b(value), .out(adder_1_out));  // open: cin, cout
endmodule

module Cnt1 (
  input  enable,
  input  clk,
  output value
);

  wire adder_1_out;

  Register #(.width(1)) register_1 (.D(adder_1_out), .en(enable), .Q(value), .clk(clk));  // open: clr
  Adder #(.width(1)) adder_1 (.a(1'b1), .b(value), .out(adder_1_out));  // open: cin, cout
endmodule

module BranchPredictor (
  input  [31:0] ir,
  input  taken,
  input  [31:0] pc,
  output [31:0] PredictAddr
);

  wire and_1_out, instructiontyper_1_beq, instructiontyper_1_bgtz, instructiontyper_1_bne,
       instructiontyper_1_jal, instructiontyper_1_jmp, or_1_out, or_2_out;
  wire [5:0] decoder_1_funct, decoder_1_op;
  wire [15:0] decoder_1_imm16;
  wire [25:0] decoder_1_imm26;
  wire [31:0] adder_1_out, addresscalculator_1_addrbranch, addresscalculator_1_addrimm, multiplexer_1_out;

  Decoder decoder_1 (
    .instruction(ir), .op(decoder_1_op), .funct(decoder_1_funct), .imm16(decoder_1_imm16),
    .imm26(decoder_1_imm26));  // open: rs, rt, rd, sham
  InstructionTyper instructiontyper_1 (
    .op(decoder_1_op), .functy(decoder_1_funct), .BEQ(instructiontyper_1_beq), .BNE(instructiontyper_1_bne),
    .JMP(instructiontyper_1_jmp), .JAL(instructiontyper_1_jal), .BGTZ(instructiontyper_1_bgtz));  // open: ADD, ADDI, ADDIU, ADDU, AND, ANDI, SLL, SRA, SRL, SUB, OR, ORI, NOR, LW, SW, SLT, SLTI, SLTU, JR, SYSCALL, DIVU, MFLO, LB
  AddressCalculator addresscalculator_1 (
    .pc(pc), .imm16(decoder_1_imm16), .imm26(decoder_1_imm26), .AddrBranch(addresscalculator_1_addrbranch),
    .AddrImm(addresscalculator_1_addrimm));
  or or_1 (or_1_out, instructiontyper_1_jmp, instructiontyper_1_jal);
  Adder #(.width(32)) adder_1 (.a(32'h4), .b(pc), .out(adder_1_out));  // open: cin, cout
  or or_2 (or_2_out, instructiontyper_1_beq, instructiontyper_1_bne, instructiontyper_1_bgtz);
  and and_1 (and_1_out, or_2_out, taken);
  Multiplexer #(.width(32), .enable("false")) multiplexer_1 (
    .in0(adder_1_out), .in1(addresscalculator_1_addrbranch), .out(multiplexer_1_out), .sel(and_1_out));
  Multiplexer #(.width(32), .enable("false")) multiplexer_2 (
    .in0(multiplexer_1_out), .in1(addresscalculator_1_addrimm), .out(PredictAddr), .sel(or_1_out));
endmodule

module AddressCalculator (
  input  [31:0] pc,
  input  [15:0] imm16,
  input  [25:0] imm26,
  output [31:0] AddrBranch,
  output [31:0] AddrImm
);

  wire [31:0] adder_1_out, bit_extender_1_out, bit_extender_2_out, shifter_1_out;
  wire [31:28] shifter_2_out;

  assign bit_extender_1_out = {{16{imm16[15]}}, imm16};  // Bit_Extender bit_extender_1
  Adder #(.width(32)) adder_1 (.a(32'h4), .b(pc), .out(adder_1_out));  // open: cin, cout
  Shifter #(.width(32)) shifter_1 (.in(bit_extender_1_out), .\dist (5'b00010), .out(shifter_1_out));
  assign bit_extender_2_out = {{6{imm26[25]}}, imm26};  // Bit_Extender bit_extender_2
  Adder #(.width(32)) adder_2 (.a(adder_1_out), .b(shifter_1_out), .out(AddrBranch));  // open: cin, cout
  Shifter #(.width(32)) shifter_2 (.in(bit_extender_2_out), .\dist (5'b00010), .out({shifter_2_out, AddrImm[27:0]}));

  assign AddrImm[31:28] = pc[31:28];
endmodule
