// Logisim project alu.circ as structural Verilog: 9 circuits, main circuit ALU
module ALU (
  input  [31:0] X,
  input  [31:0] Y,
  input  [3:0] AluOP,
  input  C0,
  input  [15:0] X_2,
  input  [15:0] Y_2,
  output Signed_Overflow,
  output UnSigned_Overflow,
  output Equal,
  output [31:0] Result,
  output [31:0] Result_2,
  output C4,
  output GS,
  output PS,
  output [15:0] out
);

  // Probe on X
  // Probe on X
  // Probe on Y
  // Probe on Y
  // Probe on AluOP
  Adder16 adder16_1 (.C4(C4), .GS(GS), .PS(PS), .S(out), .X(X_2), .Y(Y_2), .C0(C0));
  // Probe on Result
  // Probe on Result
  // Probe on Result_2

  // Other names for the same wires on the sheet: OF = Signed_Overflow; Result2[31:0] = Result_2; S[3:0] = AluOP;
  //   UOF = UnSigned_Overflow

  // Notes on the sheet:
  //   不要改变此引脚区域内容，也不要改变ALU封装形式
  //   输入引脚
  //   请在下方利用上方输入输出引脚的隧道信号构建ALU电路，ctrl+d复制选择部件
  //   华中科技大学计算机学院 计算机组成原理，鸣谢加州大学伯克利CS61C课程
  //   输出引脚
  //   探测区域
endmodule

module \演示电路  (
  input  [31:0] X,
  input  [31:0] Y,
  input  [3:0] ALUOP,
  output Signed_Overflow,
  output Unsigned_overflow,
  output [31:0] Result,
  output [31:0] Result_2,
  output Equal
);

  // Probe on X
  // Probe on X
  // ALU alu_1: pin names not known; wires that end beside it: X, Y, Signed_Overflow, ALUOP, ALUOP, Unsigned_overflow, Equal, Equal, Result, Result_2, Equal, Equal, Equal
  // Probe on ALUOP
  // Probe on Y
  // Probe on Y
  // Probe on Result
  // Probe on Result
  // Probe on Result_2

  // Notes on the sheet:
  //   ALu电路无需调整位置即可连接在该电路中，并且不能出现蓝色线缆和三态输出
endmodule

module \等差数列  (
  input  [31:0] \数列初始值 ,
  input  [31:0] \等差值 ,
  input  \时钟 ,
  output [31:0] Result
);

  // Probe on \数列初始值 
  // Probe on \数列初始值 
  // Probe on \等差值 
  // Probe on \等差值 
  // Probe on Result
  // Probe on Result

  // Other names for the same wires on the sheet: 数列初值[31:0] = \数列初始值 ; 累加和[31:0] = Result

  // Notes on the sheet:
  //   不要改变此引脚区域内容，也不要改变ALU封装形式
  //   请在下方利用上方输入输出引脚的隧道信号构建等差数列求和电路，ctrl+d复制选择部件
  //   华中科技大学计算机学院 计算机组成原理，鸣谢加州大学伯克利CS61C课程
  //   输出引脚
  //   探测区域
endmodule

module Carry_74182 (
  input  C0,
  input  [3:0] G,
  input  [3:0] P,
  output C4,
  output C3,
  output C2,
  output C1,
  output P4S,
  output G4S
);

  wire and_1_out, and_2_out, and_3_out, and_4_out, and_5_out, and_6_out, and_7_out, and_8_out, and_9_out,
       and_10_out;

  and and_1 (and_1_out, G[1], P[3], P[2]);
  and and_2 (and_2_out, G[2], P[3]);
  or or_1 (C4, G[3], and_2_out, and_1_out, and_3_out, and_4_out);
  and and_3 (and_3_out, G[0], P[3], P[2], P[1]);
  and and_4 (and_4_out, C0, P[3], P[2], P[1], P[0]);
  and and_5 (and_5_out, G[1], P[2]);
  or or_2 (C3, G[2], and_5_out, and_6_out, and_7_out);
  and and_6 (and_6_out, G[0], P[2], P[1]);
  and and_7 (and_7_out, C0, P[2], P[1], P[0]);
  GroupCarry groupcarry_1 (.G4S(G4S), .P4S(P4S), .G(G), .P(P));
  or or_3 (C2, G[1], and_8_out, and_9_out);
  and and_8 (and_8_out, G[0], P[1]);
  and and_9 (and_9_out, C0, P[1], P[0]);
  or or_4 (C1, G[0], and_10_out);
  and and_10 (and_10_out, C0, P[0]);
endmodule

module GPG (
  input  [3:0] Y,
  input  [3:0] X,
  output [3:0] G,
  output [3:0] P
);

  and and_1 (G[3], X[3], Y[3]);
  and and_2 (G[2], X[2], Y[2]);
  xor xor_1 (P[3], X[3], Y[3]);
  xor xor_2 (P[2], X[2], Y[2]);
  and and_3 (G[1], X[1], Y[1]);
  xor xor_3 (P[1], X[1], Y[1]);
  and and_4 (G[0], X[0], Y[0]);
  xor xor_4 (P[0], X[0], Y[0]);
endmodule

module Adder4_74181 (
  input  C0,
  input  [3:0] X,
  input  [3:0] Y,
  output G4S,
  output P4S,
  output C4,
  output [3:0] S
);

  wire carry_74182_1_c1, carry_74182_1_c2, carry_74182_1_c3;
  wire [3:0] gpg_1_g, gpg_1_p;

  xor xor_1 (S[3], gpg_1_p[3], carry_74182_1_c3);
  xor xor_2 (S[1], gpg_1_p[1], carry_74182_1_c1);
  xor xor_3 (S[2], gpg_1_p[2], carry_74182_1_c2);
  Carry_74182 carry_74182_1 (
    .C4(C4), .C3(carry_74182_1_c3), .C2(carry_74182_1_c2), .C1(carry_74182_1_c1), .G(gpg_1_g), .P4S(P4S),
    .G4S(G4S), .P(gpg_1_p), .C0(C0));
  GPG gpg_1 (.G(gpg_1_g), .X(X), .Y(Y), .P(gpg_1_p));
  xor xor_4 (S[0], gpg_1_p[0], C0);
endmodule

module GroupCarry (
  input  [3:0] G,
  input  [3:0] P,
  output G4S,
  output P4S
);

  wire and_1_out, and_2_out, and_3_out;

  and and_1 (and_1_out, P[3], G[2]);
  or or_1 (G4S, G[3], and_1_out, and_2_out, and_3_out);
  and and_2 (and_2_out, P[3], P[2], G[1]);
  and and_3 (and_3_out, P[3], P[2], P[1], G[0]);
  and and_4 (P4S, P[3], P[2], P[1], P[0]);
endmodule

module Adder32 (
  input  C0
);

  wire adder4_74181_6_p1;

  Adder4_74181 adder4_74181_1 ();  // open: G4S, P4S, C4, S, X, Y, C0
  Adder4_74181 adder4_74181_2 ();  // open: G4S, P4S, C4, S, X, Y, C0
  Carry_74182 carry_74182_1 ();  // open: C4, C3, C2, C1, G, P4S, G4S, P, C0
  Adder4_74181 adder4_74181_3 ();  // open: G4S, P4S, C4, S, X, Y, C0
  Adder4_74181 adder4_74181_4 ();  // open: G4S, P4S, C4, S, X, Y, C0
  Adder4_74181 adder4_74181_5 ();  // open: G4S, P4S, C4, S, X, Y, C0
  Carry_74182 carry_74182_2 (.C0(C0));  // open: C4, C3, C2, C1, G, P4S, G4S, P
  // Adder4_74181 adder4_74181_6: pin names not known; wires that end beside it: adder4_74181_6_p1, adder4_74181_6_p1
  Adder4_74181 adder4_74181_7 ();  // open: G4S, P4S, C4, S, X, Y, C0
  Adder4_74181 adder4_74181_8 (.C0(C0));  // open: G4S, P4S, C4, S, X, Y
endmodule

module Adder16 (
  input  C0,
  input  [15:0] X,
  input  [15:0] Y,
  output C4,
  output GS,
  output PS,
  output [15:0] S
);

  wire carry_74182_1_c1, carry_74182_1_c2, carry_74182_1_c3;
  wire [3:0] adder4_74181_4_g4s, adder4_74181_4_p4s;

  Adder4_74181 adder4_74181_1 (
    .G4S(adder4_74181_4_g4s[3]), .P4S(adder4_74181_4_p4s[3]), .S(S[15:12]), .X(X[15:12]), .Y(Y[15:12]),
    .C0(carry_74182_1_c3));  // open: C4
  Adder4_74181 adder4_74181_2 (
    .G4S(adder4_74181_4_g4s[2]), .P4S(adder4_74181_4_p4s[2]), .S(S[11:8]), .X(X[11:8]), .Y(Y[11:8]),
    .C0(carry_74182_1_c2));  // open: C4
  Carry_74182 carry_74182_1 (
    .C4(C4), .C3(carry_74182_1_c3), .C2(carry_74182_1_c2), .C1(carry_74182_1_c1), .G(adder4_74181_4_g4s),
    .P4S(PS), .G4S(GS), .P(adder4_74181_4_p4s), .C0(C0));
  Adder4_74181 adder4_74181_3 (
    .G4S(adder4_74181_4_g4s[1]), .P4S(adder4_74181_4_p4s[1]), .S(S[7:4]), .X(X[7:4]), .Y(Y[7:4]),
    .C0(carry_74182_1_c1));  // open: C4
  Adder4_74181 adder4_74181_4 (
    .G4S(adder4_74181_4_g4s[0]), .P4S(adder4_74181_4_p4s[0]), .S(S[3:0]), .X(X[3:0]), .Y(Y[3:0]), .C0(C0));  // open: C4
endmodule
