// Logisim project CS1409_U201414800_刘一龙_regfile.circ as structural Verilog: 4 circuits, main circuit auto_adder
module auto_adder (
  output [31:0] s0_Value,
  output [31:0] s1_Value,
  output [31:0] reg1_Value,
  output [31:0] reg2_Value
);

  wire clock_1_out, comparator_1_eq, divider_q, multiplexer_1_out, multiplexer_4_out, not_1_out;
  wire [3:0] register_1_q_2, register_1_q_3;
  wire [4:0] bit_extender_1_out, write_reg_num;
  wire [5:0] bitselector_1_out;
  wire [6:0] adder_2_out, counter_1_q, counter_2_q, multiplexer_3_out;
  wire [31:0] alu_1_result, register_1_q, sum, write_data;

  Hex_Digit_Display hex_digit_display_1 (.value(register_1_q[27:24]));  // open: dp
  Hex_Digit_Display hex_digit_display_2 (.value(register_1_q[31:28]));  // open: dp
  // Probe on write_reg_num
  // Probe on write_data
  // Probe on sum
  Hex_Digit_Display hex_digit_display_3 (.value(register_1_q_2));  // open: dp
  Hex_Digit_Display hex_digit_display_4 (.value(register_1_q_3));  // open: dp
  Register #(.width(32), .trigger("falling")) register_1 (
    .D(sum), .Q({register_1_q[31:24], register_1_q_3, register_1_q_2, register_1_q[15:0]}), .clk(divider_q));  // open: en, clr
  Clock clock_1 (.out(clock_1_out));
  Hex_Digit_Display hex_digit_display_5 (.value(register_1_q[11:8]));  // open: dp
  Hex_Digit_Display hex_digit_display_6 (.value(register_1_q[15:12]));  // open: dp
  Hex_Digit_Display hex_digit_display_7 (.value(register_1_q[3:0]));  // open: dp
  Hex_Digit_Display hex_digit_display_8 (.value(register_1_q[7:4]));  // open: dp
  Counter #(.width(1), .max('h1), .trigger("falling")) divider (
    .Q(divider_q), .clk(clock_1_out));  // open: load, D, count, carry, clr
  // Probe on s0_Value
  // Probe on s1_Value
  // Probe on reg1_Value
  // Probe on reg2_Value
  Counter #(.width(7), .max('h20), .ongoal("stay")) counter_1 (
    .Q(counter_1_q), .clk(divider_q));  // open: load, D, count, carry, clr
  assign bit_extender_1_out = {{4{1'b0}}, divider_q};  // Bit_Extender bit_extender_1
  Counter #(.width(7), .max('h41), .ongoal("stay")) counter_2 (
    .Q(counter_2_q), .clk(clock_1_out));  // open: load, D, count, carry, clr
  Adder #(.width(5)) adder_1 (.a(5'b10000), .b(bit_extender_1_out), .out(write_reg_num));  // open: cin, cout
  Comparator #(.width(7), .mode("unsigned")) comparator_1 (
    .a(7'b1000001), .b(counter_2_q), .eq(comparator_1_eq));  // open: gt, lt
  main main_1 (
    .Reg1_num(5'b10000), .Reg2(5'b10001), .Write_Reg_num(write_reg_num), .Din(write_data),
    .Write_Enable(multiplexer_1_out), .Clock(clock_1_out), .Reg1(reg1_Value), .Reg2_2(reg2_Value),
    .s0_Value(s0_Value), .s1_Value(s1_Value));  // open: s2_Value, ra_Value
  Multiplexer #(.enable("false")) multiplexer_1 (
    .in0(1'b1), .in1(1'b0), .out(multiplexer_1_out), .sel(comparator_1_eq));
  Adder #(.width(7)) adder_2 (.a(7'b0011111), .b(counter_1_q), .out(adder_2_out));  // open: cin, cout
  not not_1 (not_1_out, divider_q);
  Multiplexer #(.width(32), .enable("false")) multiplexer_2 (
    .in0(sum), .in1(alu_1_result), .out(write_data), .sel(divider_q));
  Multiplexer #(.width(7), .enable("false")) multiplexer_3 (
    .in0(adder_2_out), .in1(counter_1_q), .out(multiplexer_3_out), .sel(not_1_out));
  ALU alu_1 (
    .AluOP(4'b0101), .X(reg1_Value), .Result(alu_1_result), .Y(reg2_Value));  // open: Equal, Signed_Overflow, Result_2, UnSigned_Overflow
  BitSelector #(.width(7), .group(6)) bitselector_1 (.in(multiplexer_3_out), .out(bitselector_1_out), .sel(1'b0));
  Multiplexer #(.enable("false")) multiplexer_4 (.in0(1'b0), .in1(1'b1), .out(multiplexer_4_out), .sel(divider_q));
  RAM #(.addrWidth(6), .dataWidth(32), .bus("separate")) ram_1 (
    .addr(bitselector_1_out), .din(alu_1_result), .data(sum), .str(multiplexer_4_out),
    .sel(multiplexer_1_out), .clk(clock_1_out), .ld(1'b1));  // open: clr

  // Other names for the same wires on the sheet: reg1[31:0] = reg1_Value; reg2[31:0] = reg2_Value;
  //   s0[31:0] = s0_Value; s1[31:0] = s1_Value

  // Notes on the sheet:
  //   使能信号控制部分
  //   Debug引脚，便于观测寄存器值
  //   输出引脚
endmodule

module main (
  input  [4:0] Reg1_num,
  input  [4:0] Reg2,
  input  [4:0] Write_Reg_num,
  input  [31:0] Din,
  input  Write_Enable,
  input  Clock,
  output [31:0] Reg1,
  output [31:0] s0_Value,
  output [31:0] s1_Value,
  output [31:0] s2_Value,
  output [31:0] ra_Value,
  output [31:0] Reg2_2
);

  wire [3:0] we_selector_1_we0, we_selector_1_we1, we_selector_1_we2, we_selector_1_we3, we_selector_1_we4,
       we_selector_1_we5, we_selector_1_we6, we_selector_1_we7;
  wire [31:0] _00_q, _01_q, _02_q, _03_q, _04_q, _05_q, _06_q, _07_q, _08_q, _09_q, _10_q, _11_q, _12_q,
       _13_q, _14_q, _15_q, _19_q, _20_q, _21_q, _22_q, _23_q, _24_q, _25_q, _26_q, _27_q, _28_q, _29_q,
       _30_q;

  Register #(.width(32)) _00 (.D({32{1'b0}}), .en(we_selector_1_we0[0]), .Q(_00_q), .clk(Clock), .clr(1'b0));
  Register #(.width(32)) _08 (.D(Din), .en(we_selector_1_we0[1]), .Q(_08_q), .clk(Clock), .clr(1'b0));
  Register #(.width(32)) _16 (.D(Din), .en(we_selector_1_we0[2]), .Q(s0_Value), .clk(Clock), .clr(1'b0));
  Register #(.width(32)) _24 (.D(Din), .en(we_selector_1_we0[3]), .Q(_24_q), .clk(Clock), .clr(1'b0));
  Register #(.width(32)) _01 (.D(Din), .en(we_selector_1_we1[0]), .Q(_01_q), .clk(Clock), .clr(1'b0));
  Register #(.width(32)) _09 (.D(Din), .en(we_selector_1_we1[1]), .Q(_09_q), .clk(Clock), .clr(1'b0));
  Register #(.width(32)) _17 (.D(Din), .en(we_selector_1_we1[2]), .Q(s1_Value), .clk(Clock), .clr(1'b0));
  Register #(.width(32)) _25 (.D(Din), .en(we_selector_1_we1[3]), .Q(_25_q), .clk(Clock), .clr(1'b0));
  we_selector we_selector_1 (
    .WE(Write_Enable), .write_reg_num(Write_Reg_num), .we6(we_selector_1_we6), .we5(we_selector_1_we5),
    .we4(we_selector_1_we4), .we7(we_selector_1_we7), .we0(we_selector_1_we0), .we3(we_selector_1_we3),
    .we2(we_selector_1_we2), .we1(we_selector_1_we1));
  Register #(.width(32)) _02 (.D(Din), .en(we_selector_1_we2[0]), .Q(_02_q), .clk(Clock), .clr(1'b0));
  Register #(.width(32)) _10 (.D(Din), .en(we_selector_1_we2[1]), .Q(_10_q), .clk(Clock), .clr(1'b0));
  Register #(.width(32)) _18 (.D(Din), .en(we_selector_1_we2[2]), .Q(s2_Value), .clk(Clock), .clr(1'b0));
  Register #(.width(32)) _26 (.D(Din), .en(we_selector_1_we2[3]), .Q(_26_q), .clk(Clock), .clr(1'b0));
  Register #(.width(32)) _03 (.D(Din), .en(we_selector_1_we3[0]), .Q(_03_q), .clk(Clock), .clr(1'b0));
  Register #(.width(32)) _11 (.D(Din), .en(we_selector_1_we3[1]), .Q(_11_q), .clk(Clock), .clr(1'b0));
  Register #(.width(32)) _19 (.D(Din), .en(we_selector_1_we3[2]), .Q(_19_q), .clk(Clock), .clr(1'b0));
  Register #(.width(32)) _27 (.D(Din), .en(we_selector_1_we3[3]), .Q(_27_q), .clk(Clock), .clr(1'b0));
  Register #(.width(32)) _04 (.D(Din), .en(we_selector_1_we4[0]), .Q(_04_q), .clk(Clock), .clr(1'b0));
  Register #(.width(32)) _12 (.D(Din), .en(we_selector_1_we4[1]), .Q(_12_q), .clk(Clock), .clr(1'b0));
  Register #(.width(32)) _20 (.D(Din), .en(we_selector_1_we4[2]), .Q(_20_q), .clk(Clock), .clr(1'b0));
  Register #(.width(32)) _28 (.D(Din), .en(we_selector_1_we4[3]), .Q(_28_q), .clk(Clock), .clr(1'b0));
  Register #(.width(32)) _05 (.D(Din), .en(we_selector_1_we5[0]), .Q(_05_q), .clk(Clock), .clr(1'b0));
  Register #(.width(32)) _13 (.D(Din), .en(we_selector_1_we5[1]), .Q(_13_q), .clk(Clock), .clr(1'b0));
  Register #(.width(32)) _21 (.D(Din), .en(we_selector_1_we5[2]), .Q(_21_q), .clk(Clock), .clr(1'b0));
  Register #(.width(32)) _29 (.D(Din), .en(we_selector_1_we5[3]), .Q(_29_q), .clk(Clock), .clr(1'b0));
  Register #(.width(32)) _06 (.D(Din), .en(we_selector_1_we6[0]), .Q(_06_q), .clk(Clock), .clr(1'b0));
  Register #(.width(32)) _14 (.D(Din), .en(we_selector_1_we6[1]), .Q(_14_q), .clk(Clock), .clr(1'b0));
  Register #(.width(32)) _22 (.D(Din), .en(we_selector_1_we6[2]), .Q(_22_q), .clk(Clock), .clr(1'b0));
  Register #(.width(32)) _30 (.D(Din), .en(we_selector_1_we6[3]), .Q(_30_q), .clk(Clock), .clr(1'b0));
  Register #(.width(32)) _07 (.D(Din), .en(we_selector_1_we7[0]), .Q(_07_q), .clk(Clock), .clr(1'b0));
  Register #(.width(32)) _15 (.D(Din), .en(we_selector_1_we7[1]), .Q(_15_q), .clk(Clock), .clr(1'b0));
  Register #(.width(32)) _23 (.D(Din), .en(we_selector_1_we7[2]), .Q(_23_q), .clk(Clock), .clr(1'b0));
  Register #(.width(32)) _31 (.D(Din), .en(we_selector_1_we7[3]), .Q(ra_Value), .clk(Clock), .clr(1'b0));
  Multiplexer #(.select(5), .width(32), .enable("false")) multiplexer_1 (
    .in0(_00_q), .in1(_01_q), .in2(_02_q), .in3(_03_q), .in4(_04_q), .in5(_05_q), .in6(_06_q), .in7(_07_q),
    .in8(_08_q), .in9(_09_q), .in10(_10_q), .in11(_11_q), .in12(_12_q), .in13(_13_q), .in14(_14_q),
    .in15(_15_q), .in16(s0_Value), .in17(s1_Value), .in18(s2_Value), .in19(_19_q), .in20(_20_q),
    .in21(_21_q), .in22(_22_q), .in23(_23_q), .in24(_24_q), .in25(_25_q), .in26(_26_q), .in27(_27_q),
    .in28(_28_q), .in29(_29_q), .in30(_30_q), .in31(ra_Value), .out(Reg1), .sel(Reg1_num));
  Multiplexer #(.select(5), .width(32), .enable("false")) multiplexer_2 (
    .in0(_00_q), .in1(_01_q), .in2(_02_q), .in3(_03_q), .in4(_04_q), .in5(_05_q), .in6(_06_q), .in7(_07_q),
    .in8(_08_q), .in9(_09_q), .in10(_10_q), .in11(_11_q), .in12(_12_q), .in13(_13_q), .in14(_14_q),
    .in15(_15_q), .in16(s0_Value), .in17(s1_Value), .in18(s2_Value), .in19(_19_q), .in20(_20_q),
    .in21(_21_q), .in22(_22_q), .in23(_23_q), .in24(_24_q), .in25(_25_q), .in26(_26_q), .in27(_27_q),
    .in28(_28_q), .in29(_29_q), .in30(_30_q), .in31(ra_Value), .out(Reg2_2), .sel(Reg2));

  // Other names for the same wires on the sheet: clk = Clock; ra[31:0] = ra_Value; reg2_num[4:0] = Reg2;
  //   reg2_t[31:0] = Reg2_2; s0[31:0] = s0_Value; s1[31:0] = s1_Value; s2[31:0] = s2_Value; WE = Write_Enable;
  //   write_data[31:0] = Din

  // Notes on the sheet:
  //   输入引脚
  //   输出引脚
  //   Debug引脚，便于观测寄存器值
  //   请勿修改引脚以及封装，直接使用隧道连接电路
endmodule

module test (
  output [7:0] test_num,
  output [31:0] Reg_0_Value,
  output [31:0] Reg_1_Value,
  output [31:0] Reg_2_Value,
  output [31:0] Reg_3_Value,
  output [31:0] Read_Data_1,
  output [31:0] Read_Data_2
);

  wire clock_1_out;
  wire [7:0] adder_1_out;
  wire [15:0] rom_2_data;
  wire [31:0] WriteData;

  Register register_1 (.D(adder_1_out), .en(1'b1), .Q(test_num), .clk(clock_1_out));  // open: clr
  Adder adder_1 (.a(8'h1), .b(test_num), .out(adder_1_out));  // open: cin, cout
  ROM #(.dataWidth(32)) rom_1 (.addr(test_num), .data(WriteData));  // open: sel
  ROM #(.dataWidth(16)) rom_2 (.addr(test_num), .data(rom_2_data), .sel(1'b1));
  Clock clock_1 (.out(clock_1_out));
  main main_1 (
    .Reg1_num(rom_2_data[4:0]), .Reg2(rom_2_data[9:5]), .Write_Reg_num(rom_2_data[14:10]), .Din(WriteData),
    .Write_Enable(rom_2_data[15]), .Clock(clock_1_out), .Reg1(Read_Data_1), .Reg2_2(Read_Data_2),
    .s0_Value(Reg_0_Value), .s1_Value(Reg_1_Value), .s2_Value(Reg_2_Value), .ra_Value(Reg_3_Value));

  // Notes on the sheet:
  //   contents of rom_1 (hex, n*v repeats v):
  //   49823094 432324 4324 21321 31212 f 2121af 343e
  //   图中不应该有蓝色或红色线缆，也不应该出现未知状态 x.
  //   你的寄存器文件封装正好合适放在这里
endmodule

module we_selector (
  input  WE,
  input  [4:0] write_reg_num,
  output [3:0] we7,
  output [3:0] we0,
  output [3:0] we6,
  output [3:0] we3,
  output [3:0] we5,
  output [3:0] we2,
  output [3:0] we4,
  output [3:0] we1
);

  wire [31:0] bit_extender_1_out, demultiplexer_1_out0;

  assign bit_extender_1_out = {{31{WE}}, WE};  // Bit_Extender bit_extender_1
  assign {we7[3], we6[3], we5[3], we4[3], we3[3], we2[3], we1[3], we0[3], we7[2], we6[2], we5[2], we4[2], we3[2], we2[2], we1[2], we0[2], we7[1], we6[1], we5[1], we4[1], we3[1], we2[1], we1[1], we0[1], we7[0], we6[0], we5[0], we4[0], we3[0], we2[0], we1[0], we0[0]} = bit_extender_1_out & demultiplexer_1_out0;  // AND_Gate and_1, 32 bits wide
  Demultiplexer #(.select(5), .enable("false")) demultiplexer_1 (
    .out0(demultiplexer_1_out0[0]), .out1(demultiplexer_1_out0[1]), .out2(demultiplexer_1_out0[2]),
    .out3(demultiplexer_1_out0[3]), .out4(demultiplexer_1_out0[4]), .out5(demultiplexer_1_out0[5]),
    .out6(demultiplexer_1_out0[6]), .out7(demultiplexer_1_out0[7]), .out8(demultiplexer_1_out0[8]),
    .out9(demultiplexer_1_out0[9]), .out10(demultiplexer_1_out0[10]), .out11(demultiplexer_1_out0[11]),
    .out12(demultiplexer_1_out0[12]), .out13(demultiplexer_1_out0[13]), .out14(demultiplexer_1_out0[14]),
    .out15(demultiplexer_1_out0[15]), .out16(demultiplexer_1_out0[16]), .out17(demultiplexer_1_out0[17]),
    .out18(demultiplexer_1_out0[18]), .out19(demultiplexer_1_out0[19]), .out20(demultiplexer_1_out0[20]),
    .out21(demultiplexer_1_out0[21]), .out22(demultiplexer_1_out0[22]), .out23(demultiplexer_1_out0[23]),
    .out24(demultiplexer_1_out0[24]), .out25(demultiplexer_1_out0[25]), .out26(demultiplexer_1_out0[26]),
    .out27(demultiplexer_1_out0[27]), .out28(demultiplexer_1_out0[28]), .out29(demultiplexer_1_out0[29]),
    .out30(demultiplexer_1_out0[30]), .out31(demultiplexer_1_out0[31]), .in(1'b1), .sel(write_reg_num));
endmodule
