// Logisim project cpu.circ as structural Verilog: 8 circuits, main circuit MIPS
module MIPS (
  input  clk
);

  wire ALUSham, ALUSrc, and_1_out, and_3_out, Beq, Bne, clock_1_out, comparator_1_eq, counter_1_q,
       counter_2_q, Eq, ExtOp, Halt, Jal, Jmp, Jr, not_1_out, not_2_out, RAMtoReg, RAMWe, RegDst, RegWe,
       Syscall;
  wire [3:0] ALUOp, multiplexer_11_out_2, multiplexer_11_out_3, multiplexer_11_out_4, multiplexer_11_out_5;
  wire [4:0] multiplexer_1_out, multiplexer_2_out, multiplexer_3_out, multiplexer_4_out, rd, rs, rt, sham;
  wire [5:0] functy, op;
  wire [15:0] imm16, multiplexer_11_out;
  wire [25:0] imm26;
  wire [31:0] a0, alu_1_result, bit_extender_1_out, bit_extender_2_out, bit_extender_3_out, instruction,
       main_1_p5, main_1_p11, main_1_p13, multiplexer_5_out, multiplexer_6_out, multiplexer_7_out,
       multiplexer_8_out, multiplexer_9_out, PC, ra, ram_1_data, s0, s1, s2;

  Clock clock_1 (.out(clock_1_out));
  Counter #(.width(1), .max('h1), .ongoal("stay")) counter_1 (
    .load(1'b0), .count(1'b1), .Q(counter_1_q), .clk(Halt), .clr(1'b0));  // open: D, carry
  not not_1 (not_1_out, counter_1_q);
  // Probe on ALUOp
  // Probe on RegWe
  // Probe on ALUSrc
  // Probe on RegDst
  // Probe on ExtOp
  and and_1 (and_1_out, clock_1_out, not_1_out);
  // Probe on s0
  // Probe on s1
  Multiplexer #(.width(5), .enable("false")) multiplexer_1 (.in0(rs), .in1(rt), .out(multiplexer_1_out), .sel(ALUSham));
  Multiplexer #(.width(5), .enable("false")) multiplexer_2 (
    .in0(rt), .in1(5'b00010), .out(multiplexer_2_out), .sel(Syscall));
  Multiplexer #(.width(5), .enable("false")) multiplexer_3 (.in0(rt), .in1(rd), .out(multiplexer_3_out), .sel(RegDst));
  Multiplexer #(.width(5), .enable("false")) multiplexer_4 (
    .in0(multiplexer_3_out), .in1({5{1'b1}}), .out(multiplexer_4_out), .sel(Jal));
  IFU ifu_1 (
    .clk(and_1_out), .instruction(instruction), .Beq(Beq), .Bne(Bne), .Eq(Eq), .Jmp(Jmp), .Jr(Jr),
    .target(main_1_p11), .PC(PC), .Jal(Jal));
  // Probe on s2
  Decoder decoder_1 (
    .instruction(instruction), .op(op), .rs(rs), .rt(rt), .rd(rd), .sham(sham), .funct(functy),
    .imm16(imm16), .imm26(imm26));
  // Probe on ra
  // regfile_main main_1: pin names not known; wires that end beside it: multiplexer_1_out, multiplexer_2_out, multiplexer_4_out, s0, main_1_p5, s1, RegWe, s2, and_1_out, ra, main_1_p11, a0, main_1_p13
  // Probe on PC
  assign bit_extender_1_out = {{16{1'b0}}, imm16};  // Bit_Extender bit_extender_1
  assign bit_extender_2_out = {{16{imm16[15]}}, imm16};  // Bit_Extender bit_extender_2
  // Probe on instruction
  Multiplexer #(.width(32), .enable("false")) multiplexer_5 (
    .in0(main_1_p11), .in1(PC), .out(multiplexer_5_out), .sel(Jal));
  Multiplexer #(.width(32), .enable("false")) multiplexer_6 (
    .in0(bit_extender_1_out), .in1(bit_extender_2_out), .out(multiplexer_6_out), .sel(ExtOp));
  Multiplexer #(.width(32), .enable("false")) multiplexer_7 (
    .in0(main_1_p13), .in1(multiplexer_6_out), .out(multiplexer_7_out), .sel(ALUSrc));
  // Probe on op
  // Probe on rs
  // Probe on rt
  // Probe on rd
  // Probe on sham
  // Probe on functy
  // Probe on imm16
  // Probe on imm26
  Multiplexer #(.width(32), .enable("false")) multiplexer_8 (
    .in0(multiplexer_7_out), .in1(bit_extender_3_out), .out(multiplexer_8_out), .sel(ALUSham));
  assign bit_extender_3_out = {{27{1'b0}}, sham};  // Bit_Extender bit_extender_3
  // Probe on op
  // Probe on rs
  // Probe on rt
  // Probe on rd
  // Probe on sham
  // Probe on functy
  // Probe on imm16
  // Probe on imm26
  ControlUnit controlunit_1 (
    .op(op), .funct(functy), .ALUOp(ALUOp), .RegWe(RegWe), .ALUSrc(ALUSrc), .RegDst(RegDst), .ExtOp(ExtOp),
    .ALUSham(ALUSham), .RAMtoReg(RAMtoReg), .RAMWe(RAMWe), .Beq(Beq), .Bne(Bne), .Jmp(Jmp), .Jr(Jr),
    .Jal(Jal), .Syscall(Syscall));
  Multiplexer #(.width(32), .enable("false")) multiplexer_9 (
    .in0(multiplexer_8_out), .in1(32'h4), .out(multiplexer_9_out), .sel(Jal));
  Multiplexer #(.width(32), .enable("false")) multiplexer_10 (
    .in0(alu_1_result), .in1(ram_1_data), .out(main_1_p5), .sel(RAMtoReg));
  // Probe on op
  // Probe on rs
  // Probe on rt
  // Probe on rd
  // Probe on sham
  // Probe on functy
  // Probe on imm16
  // Probe on imm26
  ALU alu_1 (
    .AluOP(ALUOp), .X(multiplexer_5_out), .Equal(Eq), .Result(alu_1_result), .Y(multiplexer_9_out));  // open: Signed_Overflow, Result_2, UnSigned_Overflow
  Comparator #(.width(32), .mode("unsigned")) comparator_1 (
    .a(32'ha), .b(main_1_p13), .eq(comparator_1_eq));  // open: gt, lt
  Hex_Digit_Display hex_digit_display_1 (.value(multiplexer_11_out_5));  // open: dp
  and and_2 (Halt, comparator_1_eq, Syscall);
  Hex_Digit_Display hex_digit_display_2 (.value(multiplexer_11_out_4));  // open: dp
  Hex_Digit_Display hex_digit_display_3 (.value(multiplexer_11_out_3));  // open: dp
  and and_3 (and_3_out, not_2_out, Syscall);
  not not_2 (not_2_out, comparator_1_eq);
  RAM #(.addrWidth(24), .dataWidth(32), .bus("separate")) ram_1 (
    .addr(alu_1_result[25:2]), .din(main_1_p13), .data(ram_1_data), .str(RAMWe), .sel(1'b1), .clk(and_1_out),
    .ld(1'b1), .clr(1'b0));
  Hex_Digit_Display hex_digit_display_4 (.value(multiplexer_11_out[15:12]));  // open: dp
  Hex_Digit_Display hex_digit_display_5 (.value(multiplexer_11_out_2));  // open: dp
  Multiplexer #(.width(32), .enable("false")) multiplexer_11 (
    .in0({32{1'b0}}), .in1(a0),
    .out({multiplexer_11_out_5, multiplexer_11_out_4, multiplexer_11_out_3, multiplexer_11_out_2, multiplexer_11_out}),
    .sel(counter_2_q));
  Counter #(.width(1), .max('h1), .ongoal("stay")) counter_2 (
    .load(1'b0), .count(1'b1), .Q(counter_2_q), .clk(and_3_out), .clr(1'b0));  // open: D, carry
  Hex_Digit_Display hex_digit_display_6 (.value(multiplexer_11_out[7:4]));  // open: dp
  Hex_Digit_Display hex_digit_display_7 (.value(multiplexer_11_out[11:8]));  // open: dp
  Hex_Digit_Display hex_digit_display_8 (.value(multiplexer_11_out[3:0]));  // open: dp

  // Notes on the sheet:
  //   Syscall
endmodule

module IFU (
  input  [31:0] target,
  input  Bne,
  input  Jr,
  input  Eq,
  input  Beq,
  input  Jmp,
  input  Jal,
  input  clk,
  output [31:0] instruction,
  output [31:0] PC
);

  wire and_1_out, and_2_out, not_1_out, or_1_out, or_2_out;
  wire [31:0] adder_1_out, adder_2_out, bit_extender_1_out, bit_extender_2_out, multiplexer_1_out,
       multiplexer_2_out, multiplexer_3_out, shifter_1_out, shifter_2_out;

  Register #(.width(32)) u_PC (.D(multiplexer_3_out), .en(1'b1), .Q(PC), .clk(clk), .clr(1'b0));
  Adder #(.width(32)) adder_1 (.a(32'h4), .b(PC), .out(adder_1_out), .cin(1'b0));  // open: cout
  and and_1 (and_1_out, Bne, not_1_out);
  not not_1 (not_1_out, Eq);
  and and_2 (and_2_out, Beq, Eq);
  ROM #(.addrWidth(10), .dataWidth(32)) rom_1 (.addr(PC[11:2]), .data(instruction), .sel(1'b1));
  or or_1 (or_1_out, and_1_out, and_2_out);
  assign bit_extender_1_out = {{16{instruction[15]}}, instruction[15:0]};  // Bit_Extender bit_extender_1
  Adder #(.width(32)) adder_2 (.a(adder_1_out), .b(shifter_1_out), .out(adder_2_out), .cin(1'b0));  // open: cout
  Shifter #(.width(32)) shifter_1 (.in(bit_extender_1_out), .\dist (5'b00010), .out(shifter_1_out));
  assign bit_extender_2_out = {{6{instruction[25]}}, instruction[25:0]};  // Bit_Extender bit_extender_2
  Shifter #(.width(32)) shifter_2 (.in(bit_extender_2_out), .\dist (5'b00010), .out(shifter_2_out));
  Multiplexer #(.width(32), .enable("false")) multiplexer_1 (
    .in0(adder_2_out), .in1({PC[31:28], shifter_2_out[27:0]}), .out(multiplexer_1_out), .sel(or_2_out));
  or or_2 (or_2_out, Jmp, Jal);
  Multiplexer #(.width(32), .enable("false")) multiplexer_2 (
    .in0(multiplexer_1_out), .in1(target), .out(multiplexer_2_out), .sel(Jr));
  Multiplexer #(.width(32), .enable("false")) multiplexer_3 (
    .in0(adder_1_out), .in1(multiplexer_2_out), .out(multiplexer_3_out), .sel(or_1_out));

  // Notes on the sheet:
  //   /4:word => byte
  //   contents of rom_1 (hex, n*v repeats v):
  //   24100002 2411ffff 2119021 22510020 26310020 2328020 2118021 2250001f 2251000f 2118024 32120008
  //   119040 118842 241000ff 108103 2328022 2118825 365200ff 2328027 232982a ac130010 2a14000f ac140014
  //   20107fff 211a82b ac150018 20100000 ae110004 20110008 ae320004 8e100004 8e310004 2011ff9c 2012ff9c
  //   12320002 201100c8 10000001 201000e9 2011ff9c 20120064 16320002 2012012c 10000001 201100fa 20100190
  //   8000c33 20100191 20100192 20100193 20100194 20100195 201101f4 c000c3b 201101f5 201101f6 201101f7
  //   201101f8 201101f9 8000c3d 20120258 3e00008 2004007f 20020000 c 2002000a c 20100064 201100c8 2012012c
  //   PC = PC + 4 + Offset * 4
  //   PC = PC_high_4||addr||00
endmodule

module Decoder (
  input  [31:0] instruction,
  output [25:0] imm26,
  output [15:0] imm16,
  output [5:0] op,
  output [4:0] rs,
  output [4:0] rt,
  output [4:0] rd,
  output [4:0] sham,
  output [5:0] funct
);


  assign funct = instruction[5:0];
  assign imm16 = instruction[15:0];
  assign imm26 = instruction[25:0];
  assign op = instruction[31:26];
  assign rd = instruction[15:11];
  assign rs = instruction[25:21];
  assign rt = instruction[20:16];
  assign sham = instruction[10:6];

  // Notes on the sheet:
  //   R 型指令译码
  //   I 型指令译码
  //   J 型指令译码
endmodule

module InstructionTyper (
  input  [5:0] op,
  input  [5:0] funct,
  output add,
  output addi,
  output addiu,
  output addu,
  output \and ,
  output andi,
  output sll,
  output sra,
  output srl,
  output sub,
  output \or ,
  output ori,
  output \nor ,
  output lw,
  output sw,
  output beq,
  output bne,
  output slt,
  output slti,
  output sltu,
  output j,
  output jal,
  output jr,
  output syscall
);

  wire comparator_1_eq, comparator_2_eq, comparator_5_eq, comparator_6_eq, comparator_8_eq, comparator_9_eq,
       comparator_10_eq, comparator_11_eq, comparator_12_eq, comparator_14_eq, comparator_19_eq,
       comparator_21_eq, comparator_24_eq, comparator_25_eq;

  Comparator #(.width(6), .mode("unsigned")) comparator_1 (
    .a(op), .b({6{1'b0}}), .eq(comparator_1_eq));  // open: gt, lt
  Comparator #(.width(6), .mode("unsigned")) comparator_2 (
    .a(funct), .b(6'b100000), .eq(comparator_2_eq));  // open: gt, lt
  Comparator #(.width(6), .mode("unsigned")) comparator_3 (.a(op), .b(6'b001000), .eq(addi));  // open: gt, lt
  Comparator #(.width(6), .mode("unsigned")) comparator_4 (.a(op), .b(6'b001001), .eq(addiu));  // open: gt, lt
  Comparator #(.width(6), .mode("unsigned")) comparator_5 (
    .a(funct), .b(6'b100001), .eq(comparator_5_eq));  // open: gt, lt
  Comparator #(.width(6), .mode("unsigned")) comparator_6 (
    .a(funct), .b(6'b100100), .eq(comparator_6_eq));  // open: gt, lt
  Comparator #(.width(6), .mode("unsigned")) comparator_7 (.a(op), .b(6'b001100), .eq(andi));  // open: gt, lt
  Comparator #(.width(6), .mode("unsigned")) comparator_8 (
    .a(funct), .b({6{1'b0}}), .eq(comparator_8_eq));  // open: gt, lt
  Comparator #(.width(6), .mode("unsigned")) comparator_9 (
    .a(funct), .b(6'b000011), .eq(comparator_9_eq));  // open: gt, lt
  Comparator #(.width(6), .mode("unsigned")) comparator_10 (
    .a(funct), .b(6'b000010), .eq(comparator_10_eq));  // open: gt, lt
  Comparator #(.width(6), .mode("unsigned")) comparator_11 (
    .a(funct), .b(6'b100010), .eq(comparator_11_eq));  // open: gt, lt
  Comparator #(.width(6), .mode("unsigned")) comparator_12 (
    .a(funct), .b(6'b100101), .eq(comparator_12_eq));  // open: gt, lt
  Comparator #(.width(6), .mode("unsigned")) comparator_13 (.a(op), .b(6'b001101), .eq(ori));  // open: gt, lt
  Comparator #(.width(6), .mode("unsigned")) comparator_14 (
    .a(funct), .b(6'b100111), .eq(comparator_14_eq));  // open: gt, lt
  Comparator #(.width(6), .mode("unsigned")) comparator_15 (.a(op), .b(6'b100011), .eq(lw));  // open: gt, lt
  Comparator #(.width(6), .mode("unsigned")) comparator_16 (.a(op), .b(6'b101011), .eq(sw));  // open: gt, lt
  Comparator #(.width(6), .mode("unsigned")) comparator_17 (.a(op), .b(6'b000100), .eq(beq));  // open: gt, lt
  Comparator #(.width(6), .mode("unsigned")) comparator_18 (.a(op), .b(6'b000101), .eq(bne));  // open: gt, lt
  Comparator #(.width(6), .mode("unsigned")) comparator_19 (
    .a(funct), .b(6'b101010), .eq(comparator_19_eq));  // open: gt, lt
  Comparator #(.width(6), .mode("unsigned")) comparator_20 (.a(op), .b(6'b001010), .eq(slti));  // open: gt, lt
  Comparator #(.width(6), .mode("unsigned")) comparator_21 (
    .a(funct), .b(6'b101011), .eq(comparator_21_eq));  // open: gt, lt
  Comparator #(.width(6), .mode("unsigned")) comparator_22 (.a(op), .b(6'b000010), .eq(j));  // open: gt, lt
  Comparator #(.width(6), .mode("unsigned")) comparator_23 (.a(op), .b(6'b000011), .eq(jal));  // open: gt, lt
  Comparator #(.width(6), .mode("unsigned")) comparator_24 (
    .a(funct), .b(6'b001000), .eq(comparator_24_eq));  // open: gt, lt
  Comparator #(.width(6), .mode("unsigned")) comparator_25 (
    .a(funct), .b(6'b001100), .eq(comparator_25_eq));  // open: gt, lt
  and and_1 (add, comparator_1_eq, comparator_2_eq);
  and and_2 (addu, comparator_1_eq, comparator_5_eq);
  and and_3 (\and , comparator_1_eq, comparator_6_eq);
  and and_4 (sll, comparator_1_eq, comparator_8_eq);
  and and_5 (sra, comparator_1_eq, comparator_9_eq);
  and and_6 (srl, comparator_1_eq, comparator_10_eq);
  and and_7 (sub, comparator_1_eq, comparator_11_eq);
  and and_8 (\or , comparator_1_eq, comparator_12_eq);
  and and_9 (\nor , comparator_1_eq, comparator_14_eq);
  and and_10 (slt, comparator_1_eq, comparator_19_eq);
  and and_11 (sltu, comparator_1_eq, comparator_21_eq);
  and and_12 (jr, comparator_1_eq, comparator_24_eq);
  and and_13 (syscall, comparator_1_eq, comparator_25_eq);
endmodule

module InstructionTyperFaster (
  input  [5:0] op,
  input  [5:0] funct,
  output RType,
  output add,
  output addi,
  output addiu,
  output addu
);

  wire not_1_out, not_2_out, not_3_out, not_4_out, not_5_out, not_6_out, not_7_out, not_8_out, not_9_out,
       not_10_out, not_11_out, not_12_out;

  Comparator #(.width(6), .mode("unsigned")) comparator_1 (.a(op), .b({6{1'b0}}), .eq(RType));  // open: gt, lt
  not not_1 (not_1_out, op[0]);
  not not_2 (not_2_out, op[1]);
  not not_3 (not_3_out, op[2]);
  not not_4 (not_4_out, op[3]);
  not not_5 (not_5_out, op[4]);
  not not_6 (not_6_out, op[5]);
  not not_7 (not_7_out, funct[0]);
  not not_8 (not_8_out, funct[1]);
  not not_9 (not_9_out, funct[2]);
  not not_10 (not_10_out, funct[3]);
  not not_11 (not_11_out, funct[4]);
  not not_12 (not_12_out, funct[5]);
  and and_1 (add, RType, not_7_out, not_8_out, not_9_out, not_10_out, not_11_out, funct[5]);
  and and_2 (addi, not_6_out, not_5_out, op[3], not_3_out, not_2_out, not_1_out);
  and and_3 (addiu, not_6_out, not_5_out, op[3], not_3_out, not_2_out, op[0]);
  and and_4 (addu, RType, funct[5], not_11_out, not_10_out, not_9_out, not_8_out, funct[0]);
endmodule

module ControlUnit (
  input  [5:0] op,
  input  [5:0] funct,
  output [3:0] ALUOp,
  output RegWe,
  output ALUSrc,
  output RegDst,
  output ExtOp,
  output ALUSham,
  output RAMtoReg,
  output RAMWe,
  output Beq,
  output Bne,
  output Jmp,
  output Jal,
  output Jr,
  output Syscall
);

  wire instructiontyper_1_add, instructiontyper_1_addi, instructiontyper_1_addiu, instructiontyper_1_addu,
       instructiontyper_1_and, instructiontyper_1_andi, instructiontyper_1_beq, instructiontyper_1_bne,
       instructiontyper_1_nor, instructiontyper_1_or, instructiontyper_1_ori, instructiontyper_1_sll,
       instructiontyper_1_slt, instructiontyper_1_slti, instructiontyper_1_sltu, instructiontyper_1_sra,
       instructiontyper_1_srl, instructiontyper_1_sub;

  InstructionTyper instructiontyper_1 (
    .op(op), .funct(funct), .add(instructiontyper_1_add), .addi(instructiontyper_1_addi),
    .addiu(instructiontyper_1_addiu), .addu(instructiontyper_1_addu), .\and (instructiontyper_1_and),
    .andi(instructiontyper_1_andi), .sll(instructiontyper_1_sll), .sra(instructiontyper_1_sra),
    .srl(instructiontyper_1_srl), .sub(instructiontyper_1_sub), .\or (instructiontyper_1_or),
    .ori(instructiontyper_1_ori), .\nor (instructiontyper_1_nor), .lw(RAMtoReg), .sw(RAMWe),
    .beq(instructiontyper_1_beq), .bne(instructiontyper_1_bne), .slt(instructiontyper_1_slt),
    .slti(instructiontyper_1_slti), .sltu(instructiontyper_1_sltu), .j(Jmp), .jal(Jal), .jr(Jr),
    .syscall(Syscall));
  or or_1 (ALUOp[0], instructiontyper_1_add, instructiontyper_1_addi, instructiontyper_1_addiu, instructiontyper_1_addu, instructiontyper_1_and, instructiontyper_1_andi, instructiontyper_1_sra, RAMtoReg, RAMWe, instructiontyper_1_slt, instructiontyper_1_slti, Jal);
  or or_2 (ALUOp[1], instructiontyper_1_and, instructiontyper_1_andi, instructiontyper_1_srl, instructiontyper_1_sub, instructiontyper_1_nor, instructiontyper_1_slt, instructiontyper_1_slti);
  or or_3 (ALUOp[2], instructiontyper_1_add, instructiontyper_1_addi, instructiontyper_1_addiu, instructiontyper_1_addu, instructiontyper_1_and, instructiontyper_1_andi, instructiontyper_1_sub, RAMtoReg, RAMWe, instructiontyper_1_sltu, Jal);
  or or_4 (ALUOp[3], instructiontyper_1_or, instructiontyper_1_ori, instructiontyper_1_nor, instructiontyper_1_slt, instructiontyper_1_slti, instructiontyper_1_sltu);
  or or_5 (RegWe, instructiontyper_1_add, instructiontyper_1_addi, instructiontyper_1_addiu, instructiontyper_1_addu, instructiontyper_1_and, instructiontyper_1_andi, instructiontyper_1_sll, instructiontyper_1_sra, instructiontyper_1_srl, instructiontyper_1_sub, instructiontyper_1_or, instructiontyper_1_ori, instructiontyper_1_nor, RAMtoReg, instructiontyper_1_slt, instructiontyper_1_slti, instructiontyper_1_sltu, Jal);
  or or_6 (ALUSrc, instructiontyper_1_addi, instructiontyper_1_addiu, instructiontyper_1_andi, instructiontyper_1_ori, RAMtoReg, RAMWe, instructiontyper_1_slti);
  or or_7 (RegDst, instructiontyper_1_add, instructiontyper_1_addu, instructiontyper_1_and, instructiontyper_1_sll, instructiontyper_1_sra, instructiontyper_1_srl, instructiontyper_1_sub, instructiontyper_1_or, instructiontyper_1_nor, instructiontyper_1_slt, instructiontyper_1_sltu);
  or or_8 (ExtOp, instructiontyper_1_addi, instructiontyper_1_andi, instructiontyper_1_ori, RAMtoReg, RAMWe, instructiontyper_1_slti);
  or or_9 (ALUSham, instructiontyper_1_sll, instructiontyper_1_sra, instructiontyper_1_srl);
  or or_10 (Beq, instructiontyper_1_beq, Jmp, Jal, Jr);
  or or_11 (Bne, instructiontyper_1_bne, Jmp, Jal, Jr);
endmodule

module main (
  input  [31:0] INSTRUCTION,
  input  CLOCK,
  output [31:0] FETCH_ADDRESS,
  output [31:0] s0_Value,
  output [31:0] s1_Value,
  output [31:0] s2_Value,
  output [31:0] ra_Value,
  output [31:0] sp_Value,
  output [31:0] HI_Value,
  output [31:0] LO_Value
);

  Register #(.width(32)) PC ();  // open: D, en, Q, clk, clr
  Register #(.width(32)) LO ();  // open: D, en, Q, clk, clr
  Register #(.width(32)) HI ();  // open: D, en, Q, clk, clr

  // Other names for the same wires on the sheet: clk = CLOCK; fetch_addr[31:0] = FETCH_ADDRESS

  // Notes on the sheet:
  //   Output
  //   Inputs
endmodule

module Analysis (
  input  Beq,
  input  Bne,
  input  Eq,
  output PC
);

  wire and_1_out, and_2_out, not_1_out;

  not not_1 (not_1_out, Eq);
  and and_1 (and_1_out, Bne, not_1_out);
  and and_2 (and_2_out, Beq, Eq);
  or or_1 (PC, and_1_out, and_2_out);
endmodule
