// Logisim project CPU-branches.circ as structural Verilog: 1 circuit, main circuit main
module main (
  output [31:0] Reg_0_Value,
  output [31:0] Reg_1_Value,
  output [31:0] Reg_2_Value,
  output [31:0] Reg_3_Value,
  output [31:0] Reg_sp_Value,
  output [31:0] Reg_HI_Value,
  output [31:0] Reg_LO_Value,
  output [31:0] Time_Step,
  output [31:0] Requested_Address,
  output [31:0] Requested_Instruction
);

  wire clock_1_out;

  Clock clock_1 (.out(clock_1_out));
  cpu_main main_1 (
    .INSTRUCTION(Requested_Instruction), .CLOCK(clock_1_out), .FETCH_ADDRESS(Requested_Address),
    .s0_Value(Reg_0_Value), .s1_Value(Reg_1_Value), .s2_Value(Reg_2_Value), .ra_Value(Reg_3_Value),
    .sp_Value(Reg_sp_Value), .HI_Value(Reg_HI_Value), .LO_Value(Reg_LO_Value));
  Counter #(.width(32), .max('hffffffff)) counter_1 (
    .Q(Time_Step), .clk(clock_1_out));  // open: load, D, count, carry, clr
  // Probe on Requested_Address
  ROM #(.addrWidth(24), .dataWidth(32)) rom_1 (
    .addr(Requested_Address[25:2]), .data(Requested_Instruction));  // open: sel
  // Probe on Requested_Instruction

  // Other names for the same wires on the sheet: fetch_addr[31:0] = Requested_Address;
  //   Instruction[31:0] = Requested_Instruction

  // Notes on the sheet:
  //   YOUR CPU SHOULD FIT IN HERE!
  //   There should be no blue/red wires here, and the outputs shouldn't be x's.
  //   Instruction Memory
  //   contents of rom_1 (hex, n*v repeats v):
  //   16100001 12100004 3c1000ff 1210fffe 24100002 16110003 24100001 1a11fffc 1211fffd 24100004 1650ffff
  //   3612ffff
endmodule
