// Logisim project 74670.circ as structural Verilog: 1 circuit, main circuit 74670
module _74670 (
  input  Gr,
  input  Ra,
  input  Rb,
  input  [3:0] D,
  input  Gw,
  input  Wa,
  input  Wb,
  output [3:0] Q
);

  wire decoder_1_out0, decoder_1_out1, decoder_1_out2, decoder_1_out3, not_1_out, not_2_out;
  wire [3:0] register_1_q, register_2_q, register_3_q, register_4_q;

  not not_1 (not_1_out, Gw);
  Decoder #(.select(2), .disabled(0), .enable("false")) decoder_1 (
    .out0(decoder_1_out0), .out1(decoder_1_out1), .out2(decoder_1_out2), .out3(decoder_1_out3), .sel({Wb, Wa}));
  Register #(.width(4), .trigger("high")) register_1 (
    .D(D), .en(not_1_out), .Q(register_1_q), .clk(decoder_1_out0));  // open: clr
  Register #(.width(4), .trigger("high")) register_2 (
    .D(D), .en(not_1_out), .Q(register_2_q), .clk(decoder_1_out1));  // open: clr
  Register #(.width(4), .trigger("high")) register_3 (
    .D(D), .en(not_1_out), .Q(register_3_q), .clk(decoder_1_out2));  // open: clr
  not not_2 (not_2_out, Gr);
  Multiplexer #(.select(2), .width(4)) multiplexer_1 (
    .in0(register_1_q), .in1(register_2_q), .in2(register_3_q), .in3(register_4_q), .out(Q), .sel({Rb, Ra}),
    .en(not_2_out));
  Register #(.width(4), .trigger("high")) register_4 (
    .D(D), .en(not_1_out), .Q(register_4_q), .clk(decoder_1_out3));  // open: clr
endmodule
