// Logisim project cpu.circ as structural Verilog: 1 circuit, main circuit main
module main (
  input  [31:0] INSTRUCTION,
  input  CLOCK,
  output [31:0] FETCH_ADDRESS,
  output [31:0] s0_Value,
  output [31:0] s1_Value,
  output [31:0] s2_Value,
  output [31:0] ra_Value,
  output [31:0] sp_Value,
  output [31:0] HI_Value,
  output [31:0] LO_Value
);

  wire main_2_p1, main_2_p2, main_2_p4, main_2_p5, main_2_p7, main_2_p10;

  Register #(.width(32)) PC ();  // open: D, en, Q, clk, clr
  Register #(.width(32)) HI ();  // open: D, en, Q, clk, clr
  Register #(.width(32)) LO ();  // open: D, en, Q, clk, clr
  // regfile_main main_1: pin names not known
  // alu_main main_2: pin names not known; wires that end beside it: main_2_p1, main_2_p2, main_2_p2, main_2_p4, main_2_p5, s0_Value, main_2_p7, main_2_p7, s1_Value, main_2_p10
  // mem_main MEM: pin names not known

  // Other names for the same wires on the sheet: clk = CLOCK; fetch_addr[31:0] = FETCH_ADDRESS

  // Notes on the sheet:
  //   Output
  //   These are outputs/inputs from run.circ
  //   Inputs
  //   These are DEBUG/TEST outputs from your circuit.
endmodule
